// Logisim project RISC-V.circ as structural Verilog: 19 circuits, main circuit main
module main (
  input  CLK,
  output [4:0] out_2,
  output [1:0] out_3,
  output [2:0] out_4,
  output out_5,
  output [1:0] out_6,
  output [1:0] out_7,
  output out_8,
  output out_9,
  output out_10,
  output [1:0] out_11,
  output out_12,
  output out_13,
  output out_14,
  output out_15,
  output out_16
);

  wire CLK_t, CLR_regs, csr_1_stop_clock, CSRIllegal, Exception, exceptions_1_interrupt, i_o_1_clk_2,
       i_o_1_clk_3, i_o_1_clr_2, i_o_1_clr_3, i_o_1_enable_keyboard, i_o_1_enable_tty, i_o_1_in_range,
       i_o_1_misaligned, InstrAddrMisaligned, keyboard_1_avail, memory_1_i_o_read, Start_out, Stop_out;
  wire [1:0] Interrupts, PI;
  wire [2:0] compare_1_flags, split_instruction_1_func3;
  wire [4:0] MemExcept, split_instruction_1_rd, split_instruction_1_rs1, split_instruction_1_rs2;
  wire [6:0] split_instruction_1_func7, split_instruction_1_opcode;
  wire [11:0] split_instruction_1_csr_specifier;
  wire [15:0] i_o_1_tty_data, keyboard_1_data;
  wire [31:0] add_4_1_output, alu_1_result, csr_1_newpc, csr_1_output, exceptions_1_cause, exceptions_1_val,
       i_o_1_data_out, i_o_1_screen_1, i_o_1_screen_2, i_o_1_screen_3, i_o_1_screen_4, i_o_1_screen_5,
       i_o_1_screen_6, i_o_1_screen_7, i_o_1_screen_8, i_o_1_screen_9, i_o_1_screen_10, i_o_1_screen_11,
       i_o_1_screen_12, i_o_1_screen_13, i_o_1_screen_14, i_o_1_screen_15, i_o_1_screen_16, i_o_1_screen_17,
       i_o_1_screen_18, i_o_1_screen_19, i_o_1_screen_20, i_o_1_screen_21, i_o_1_screen_22, i_o_1_screen_23,
       i_o_1_screen_24, i_o_1_screen_25, i_o_1_screen_26, i_o_1_screen_27, i_o_1_screen_28, i_o_1_screen_29,
       i_o_1_screen_30, i_o_1_screen_31, i_o_1_screen_32, memory_1_data, memory_1_i_o_address,
       memory_1_instruction, multiplexer_1_out, multiplexer_2_out, multiplexer_3_out, pc_1_pc,
       register_file_1_read_data_1, register_file_1_read_data_2, split_instruction_1_imm_b,
       split_instruction_1_imm_i, split_instruction_1_imm_j, split_instruction_1_imm_s,
       split_instruction_1_imm_u, \time , timeh;

  PC pc_1 (
    .Jump_Addr(alu_1_result), .PC(pc_1_pc), .Jump(out_10), .CLK(CLK_t), .RST(CLR_regs),
    .Exception_Jump_Addr(csr_1_newpc), .Exception(Exception),
    .Instruction_adress_misaligned(InstrAddrMisaligned), .Mret(out_16));
  Keyboard #(.Char_bit_width(16), .buflen(256), .trigger("falling")) keyboard_1 (
    .clk(i_o_1_clk_2), .re(i_o_1_enable_keyboard), .clr(i_o_1_clr_2), .avail(keyboard_1_avail),
    .data(keyboard_1_data));
  I_O i_o_1 (
    .CLK_2(i_o_1_clk_2), .Enable_Keyboard(i_o_1_enable_keyboard), .CLR_2(i_o_1_clr_2),
    .Keyboard_Available(keyboard_1_avail), .Keyboard_Data(keyboard_1_data), .TTY_Data(i_o_1_tty_data),
    .CLK_3(i_o_1_clk_3), .Enable_TTY(i_o_1_enable_tty), .CLR_3(i_o_1_clr_3), .Screen_1(i_o_1_screen_1),
    .Screen_2(i_o_1_screen_2), .Screen_3(i_o_1_screen_3), .Screen_4(i_o_1_screen_4),
    .Screen_5(i_o_1_screen_5), .Screen_6(i_o_1_screen_6), .Screen_7(i_o_1_screen_7),
    .Screen_8(i_o_1_screen_8), .Screen_9(i_o_1_screen_9), .Screen_10(i_o_1_screen_10),
    .Screen_11(i_o_1_screen_11), .Screen_12(i_o_1_screen_12), .Screen_13(i_o_1_screen_13),
    .Screen_14(i_o_1_screen_14), .Screen_15(i_o_1_screen_15), .Screen_16(i_o_1_screen_16),
    .Screen_17(i_o_1_screen_17), .Screen_18(i_o_1_screen_18), .Screen_19(i_o_1_screen_19),
    .Screen_20(i_o_1_screen_20), .Screen_21(i_o_1_screen_21), .Screen_22(i_o_1_screen_22),
    .Screen_23(i_o_1_screen_23), .Screen_24(i_o_1_screen_24), .Screen_25(i_o_1_screen_25),
    .Screen_26(i_o_1_screen_26), .Screen_27(i_o_1_screen_27), .Screen_28(i_o_1_screen_28),
    .Screen_29(i_o_1_screen_29), .Screen_30(i_o_1_screen_30), .Screen_31(i_o_1_screen_31),
    .Screen_32(i_o_1_screen_32), .Data_out(i_o_1_data_out), .Misaligned(i_o_1_misaligned),
    .In_range(i_o_1_in_range), .Data_in(register_file_1_read_data_2), .Address(memory_1_i_o_address),
    .CLK(CLK_t), .CLR(CLR_regs), .Write(out_8), .DataSize(out_6), .Read(memory_1_i_o_read), .\time (\time ),
    .timeh(timeh), .Pending_interrupts(PI));
  Memory memory_1 (
    .Write_Data(register_file_1_read_data_2), .PC(pc_1_pc), .Data_addr(alu_1_result), .Data(memory_1_data),
    .Instruction(memory_1_instruction), .I_O_Address(memory_1_i_o_address), .I_O_Data(i_o_1_data_out),
    .I_O_In_Range(i_o_1_in_range), .I_O_misaligned(i_o_1_misaligned), .CLK(CLK_t), .Write(out_8),
    .Data_Src(out_7), .Signed__Unsigned(out_5), .Data_size(out_6), .CLR_regs(CLR_regs),
    .Exceptions(MemExcept), .Exception(Exception), .I_O_read(memory_1_i_o_read));
  TTY #(.Char_bit_width(16), .rows(16), .cols(40), .trigger("falling")) tty_1 (
    .data(i_o_1_tty_data), .clk(i_o_1_clk_3), .we(i_o_1_enable_tty), .clr(i_o_1_clr_3));
  Split_instruction split_instruction_1 (
    .Instruction(memory_1_instruction), .Opcode(split_instruction_1_opcode),
    .Func3(split_instruction_1_func3), .Func7(split_instruction_1_func7), .Rd(split_instruction_1_rd),
    .Rs1(split_instruction_1_rs1), .Rs2(split_instruction_1_rs2), .Imm_I(split_instruction_1_imm_i),
    .Imm_S(split_instruction_1_imm_s), .Imm_B(split_instruction_1_imm_b), .Imm_U(split_instruction_1_imm_u),
    .Imm_J(split_instruction_1_imm_j), .CSR_Specifier(split_instruction_1_csr_specifier));
  Exceptions exceptions_1 (
    .InstrAddrMisaligned(InstrAddrMisaligned), .Ecall(out_14), .Ebreak(out_15), .IllegalInstr(out_13),
    .CSRIllegal(CSRIllegal), .MemExcept(MemExcept), .Cause(exceptions_1_cause), .Exception(Exception),
    .Interrupt(exceptions_1_interrupt), .ALUVal(alu_1_result), .Instruction(memory_1_instruction),
    .Val(exceptions_1_val), .PC(pc_1_pc), .Interrupts(Interrupts));
  Control control_1 (
    .Opcode(split_instruction_1_opcode), .Func3(split_instruction_1_func3),
    .Func7(split_instruction_1_func7), .ALU_op(out_2), .ALU_Src1(out_3), .DataSrc(out_7), .RegWrite(out_9),
    .Jump(out_10), .ALU_Src2(out_4), .Flags(compare_1_flags), .RAMWrite(out_8), .DataSize(out_6),
    .DataSign(out_5), .CSR_Op(out_11), .CSR_Imm(out_12), .Ecall(out_14), .Ebreak(out_15),
    .Illegal_instruction(out_13), .Instruction(memory_1_instruction), .Mret(out_16));
  DotMatrix #(.inputtype("row"), .matrixcols(32), .matrixrows(32)) dotmatrix_1 (
    .row0(i_o_1_screen_1), .row1(i_o_1_screen_2), .row2(i_o_1_screen_3), .row3(i_o_1_screen_4),
    .row4(i_o_1_screen_5), .row5(i_o_1_screen_6), .row6(i_o_1_screen_7), .row7(i_o_1_screen_8),
    .row8(i_o_1_screen_9), .row9(i_o_1_screen_10), .row10(i_o_1_screen_11), .row11(i_o_1_screen_12),
    .row12(i_o_1_screen_13), .row13(i_o_1_screen_14), .row14(i_o_1_screen_15), .row15(i_o_1_screen_16),
    .row16(i_o_1_screen_17), .row17(i_o_1_screen_18), .row18(i_o_1_screen_19), .row19(i_o_1_screen_20),
    .row20(i_o_1_screen_21), .row21(i_o_1_screen_22), .row22(i_o_1_screen_23), .row23(i_o_1_screen_24),
    .row24(i_o_1_screen_25), .row25(i_o_1_screen_26), .row26(i_o_1_screen_27), .row27(i_o_1_screen_28),
    .row28(i_o_1_screen_29), .row29(i_o_1_screen_30), .row30(i_o_1_screen_31), .row31(i_o_1_screen_32));
  Add_4 add_4_1 (.Input(pc_1_pc), .Output(add_4_1_output));
  CSR csr_1 (
    .Illegal_instruction(CSRIllegal), .NewPC(csr_1_newpc), .Interrupt(exceptions_1_interrupt),
    .Val(exceptions_1_val), .Cause(exceptions_1_cause), .PC(pc_1_pc), .Exception(Exception),
    .Return_from_exception(out_16), .Rs1_uimm(split_instruction_1_rs1), .Rd(split_instruction_1_rd),
    .CSR_specifier(split_instruction_1_csr_specifier), .Output(csr_1_output), .\time (\time ), .timeh(timeh),
    .Rs1Val(register_file_1_read_data_1), .Operation____RW_RS_RC(out_11), .DataSrc(out_7), .CLK(CLK_t),
    .CLR(CLR_regs), .Imm(out_12), .Pending_interrupts(PI), .Interrupts(Interrupts),
    .Stop_clock(csr_1_stop_clock));
  Multiplexer #(.select(2), .width(32), .enable("false")) multiplexer_1 (
    .in0(memory_1_data), .in1(alu_1_result), .in2(add_4_1_output), .in3(csr_1_output),
    .out(multiplexer_1_out), .sel(out_7));
  Compare compare_1 (.Flags(compare_1_flags), .Rs1(register_file_1_read_data_1), .Rs2(register_file_1_read_data_2));
  Register_File register_file_1 (
    .Read_Data_1(register_file_1_read_data_1), .Read_Data_2(register_file_1_read_data_2),
    .Read_Reg_1(split_instruction_1_rs1), .Read_Reg_2(split_instruction_1_rs2),
    .Write_Reg(split_instruction_1_rd), .Write_data(multiplexer_1_out), .RegWrite(out_9), .CLK(CLK_t),
    .CLR(CLR_regs), .Exception(Exception));
  CLK clk_1 (
    .Stop_clock(csr_1_stop_clock), .CLK(CLK_t), .CLR(CLR_regs), .Start(Start_out), .Manual(CLK),
    .Stop(Stop_out));
  Button Reset (.out(CLR_regs));
  Button Stop (.out(Stop_out));
  Button Start (.out(Start_out));
  Multiplexer #(.select(2), .width(32), .enable("false")) multiplexer_2 (
    .in0(register_file_1_read_data_1), .in1(split_instruction_1_imm_u), .in2(split_instruction_1_imm_j),
    .in3(split_instruction_1_imm_b), .out(multiplexer_2_out), .sel(out_3));
  Multiplexer #(.select(3), .width(32), .enable("false")) multiplexer_3 (
    .in0({32{1'b0}}), .in1(register_file_1_read_data_2), .in2(split_instruction_1_imm_i), .in3(pc_1_pc),
    .in4(split_instruction_1_imm_s), .out(multiplexer_3_out), .sel(out_4));  // open: in5, in6, in7
  ALU alu_1 (.Operand1(multiplexer_2_out), .Operand2(multiplexer_3_out), .Operation(out_2), .Result(alu_1_result));

  // Other names for the same wires on the sheet: ALU_op[4:0] = out_2; ALU_Src1[1:0] = out_3; ALU_Src2[2:0] = out_4;
  //   CSR_Imm = out_12; CSR_Op[1:0] = out_11; Data_Sign = out_5; Data_Size[1:0] = out_6; Data_Src[1:0] = out_7;
  //   Ebreak = out_15; Ecall = out_14; IllegalInstr = out_13; Jump = out_10; Mret = out_16; RAMWrite = out_8;
  //   RegWrite = out_9

  // Notes on the sheet:
  //   Data-Src: RAM, ALU, PC, CSR
  //   ALU-Src1: Reg, Imm-U, Imm-J, Imm-B
  //   ALU-Src2: Zero, Reg, Imm-I, PC, Imm-S
endmodule

module PC (
  input  [31:0] Jump_Addr,
  input  [31:0] Exception_Jump_Addr,
  input  Mret,
  input  Exception,
  input  Jump,
  input  CLK,
  input  RST,
  output Instruction_adress_misaligned,
  output [31:0] PC
);

  wire and_1_out, and_2_out, buffer_1_out, buffer_2_out, buffer_3_out, nor_1_out, not_1_out, not_2_out,
       or_2_out, or_3_out, or_4_out;
  wire [31:0] multiplexer_1_out, multiplexer_2_out;

  Pull_Resistor pull_resistor_1 (.node(Jump_Addr[1]));
  or or_1 (Instruction_adress_misaligned, and_1_out, and_2_out);
  and and_1 (and_1_out, Jump_Addr[1], Jump);
  and and_2 (and_2_out, or_3_out, Exception_Jump_Addr[1]);
  Pull_Resistor pull_resistor_2 (.node(Exception_Jump_Addr[1]));
  Multiplexer #(.width(32), .enable("false")) multiplexer_1 (
    .in0(Jump_Addr), .in1(Exception_Jump_Addr), .out(multiplexer_1_out), .sel(or_3_out));
  or or_2 (or_2_out, or_3_out, Jump, buffer_1_out);
  or or_3 (or_3_out, Mret, Exception);
  Multiplexer #(.width(32), .enable("false")) multiplexer_2 (
    .in0(multiplexer_1_out), .in1(32'h400000), .out(multiplexer_2_out), .sel(buffer_1_out));
  buf buffer_1 (buffer_1_out, buffer_2_out);
  buf buffer_2 (buffer_2_out, buffer_3_out);
  buf buffer_3 (buffer_3_out, RST);
  Counter #(.width(30), .max('h3fffffff), .trigger("falling"), .behavior("old")) counter_1 (
    .load(or_2_out), .D(multiplexer_2_out[31:2]), .count(not_1_out), .Q(PC[31:2]), .clk(or_4_out));  // open: carry, clr, preset
  not not_1 (not_1_out, or_2_out);
  or or_4 (or_4_out, CLK, nor_1_out);
  nor nor_1 (nor_1_out, not_2_out, RST);
  not not_2 (not_2_out, RST);

  assign PC[1:0] = 2'b00;

  // Notes on the sheet:
  //   Last two bits must always be 0, so discard them everywhere
  //   Start Address
endmodule

module Register_File (
  input  [4:0] Read_Reg_1,
  input  [4:0] Read_Reg_2,
  input  [4:0] Write_Reg,
  input  [31:0] Write_data,
  input  RegWrite,
  input  Exception,
  input  CLK,
  input  CLR,
  output [31:0] Read_Data_1,
  output [31:0] Read_Data_2
);

  wire and_1_out, decoder_1_out0, decoder_1_out1, decoder_1_out2, decoder_1_out3, decoder_1_out4,
       decoder_1_out5, decoder_1_out6, decoder_1_out7, decoder_1_out8, decoder_1_out9, decoder_1_out10,
       decoder_1_out11, decoder_1_out12, decoder_1_out13, decoder_1_out14, decoder_1_out15, decoder_1_out16,
       decoder_1_out17, decoder_1_out18, decoder_1_out19, decoder_1_out20, decoder_1_out21, decoder_1_out22,
       decoder_1_out23, decoder_1_out24, decoder_1_out25, decoder_1_out26, decoder_1_out27, decoder_1_out28,
       decoder_1_out29, decoder_1_out30, decoder_1_out31;
  wire [31:0] register_1_q, register_2_q, register_3_q, register_4_q, register_5_q, register_6_q,
       register_7_q, register_8_q, register_9_q, register_10_q, register_11_q, register_12_q, register_13_q,
       register_14_q, register_15_q, register_16_q, register_17_q, register_18_q, register_19_q,
       register_20_q, register_21_q, register_22_q, register_23_q, register_24_q, register_25_q,
       register_26_q, register_27_q, register_28_q, register_29_q, register_30_q, register_31_q;

  and and_1 (and_1_out, RegWrite, ~Exception);  // AND_Gate
  Decoder #(.select(5), .disabled(0)) decoder_1 (
    .out0(decoder_1_out0), .out1(decoder_1_out1), .out2(decoder_1_out2), .out3(decoder_1_out3),
    .out4(decoder_1_out4), .out5(decoder_1_out5), .out6(decoder_1_out6), .out7(decoder_1_out7),
    .out8(decoder_1_out8), .out9(decoder_1_out9), .out10(decoder_1_out10), .out11(decoder_1_out11),
    .out12(decoder_1_out12), .out13(decoder_1_out13), .out14(decoder_1_out14), .out15(decoder_1_out15),
    .out16(decoder_1_out16), .out17(decoder_1_out17), .out18(decoder_1_out18), .out19(decoder_1_out19),
    .out20(decoder_1_out20), .out21(decoder_1_out21), .out22(decoder_1_out22), .out23(decoder_1_out23),
    .out24(decoder_1_out24), .out25(decoder_1_out25), .out26(decoder_1_out26), .out27(decoder_1_out27),
    .out28(decoder_1_out28), .out29(decoder_1_out29), .out30(decoder_1_out30), .out31(decoder_1_out31),
    .sel(Write_Reg), .en(and_1_out));
  Register #(.width(32), .trigger("falling"), .Select("low")) register_1 (
    .D(Write_data), .en(decoder_1_out1), .Q(register_1_q), .clk(CLK), .clr(CLR));
  Register #(.width(32), .trigger("falling"), .Select("low")) register_2 (
    .D(Write_data), .en(decoder_1_out2), .Q(register_2_q), .clk(CLK), .clr(CLR));
  Register #(.width(32), .trigger("falling"), .Select("low")) register_3 (
    .D(Write_data), .en(decoder_1_out3), .Q(register_3_q), .clk(CLK), .clr(CLR));
  Register #(.width(32), .trigger("falling"), .Select("low")) register_4 (
    .D(Write_data), .en(decoder_1_out4), .Q(register_4_q), .clk(CLK), .clr(CLR));
  Register #(.width(32), .trigger("falling"), .Select("low")) register_5 (
    .D(Write_data), .en(decoder_1_out5), .Q(register_5_q), .clk(CLK), .clr(CLR));
  Register #(.width(32), .trigger("falling"), .Select("low")) register_6 (
    .D(Write_data), .en(decoder_1_out6), .Q(register_6_q), .clk(CLK), .clr(CLR));
  Register #(.width(32), .trigger("falling"), .Select("low")) register_7 (
    .D(Write_data), .en(decoder_1_out7), .Q(register_7_q), .clk(CLK), .clr(CLR));
  Register #(.width(32), .trigger("falling"), .Select("low")) register_8 (
    .D(Write_data), .en(decoder_1_out8), .Q(register_8_q), .clk(CLK), .clr(CLR));
  Register #(.width(32), .trigger("falling"), .Select("low")) register_9 (
    .D(Write_data), .en(decoder_1_out9), .Q(register_9_q), .clk(CLK), .clr(CLR));
  Register #(.width(32), .trigger("falling"), .Select("low")) register_10 (
    .D(Write_data), .en(decoder_1_out10), .Q(register_10_q), .clk(CLK), .clr(CLR));
  Register #(.width(32), .trigger("falling"), .Select("low")) register_11 (
    .D(Write_data), .en(decoder_1_out11), .Q(register_11_q), .clk(CLK), .clr(CLR));
  Register #(.width(32), .trigger("falling"), .Select("low")) register_12 (
    .D(Write_data), .en(decoder_1_out12), .Q(register_12_q), .clk(CLK), .clr(CLR));
  Register #(.width(32), .trigger("falling"), .Select("low")) register_13 (
    .D(Write_data), .en(decoder_1_out13), .Q(register_13_q), .clk(CLK), .clr(CLR));
  Register #(.width(32), .trigger("falling"), .Select("low")) register_14 (
    .D(Write_data), .en(decoder_1_out14), .Q(register_14_q), .clk(CLK), .clr(CLR));
  Register #(.width(32), .trigger("falling"), .Select("low")) register_15 (
    .D(Write_data), .en(decoder_1_out15), .Q(register_15_q), .clk(CLK), .clr(CLR));
  Register #(.width(32), .trigger("falling"), .Select("low")) register_16 (
    .D(Write_data), .en(decoder_1_out16), .Q(register_16_q), .clk(CLK), .clr(CLR));
  Register #(.width(32), .trigger("falling"), .Select("low")) register_17 (
    .D(Write_data), .en(decoder_1_out17), .Q(register_17_q), .clk(CLK), .clr(CLR));
  Register #(.width(32), .trigger("falling"), .Select("low")) register_18 (
    .D(Write_data), .en(decoder_1_out18), .Q(register_18_q), .clk(CLK), .clr(CLR));
  Register #(.width(32), .trigger("falling"), .Select("low")) register_19 (
    .D(Write_data), .en(decoder_1_out19), .Q(register_19_q), .clk(CLK), .clr(CLR));
  Register #(.width(32), .trigger("falling"), .Select("low")) register_20 (
    .D(Write_data), .en(decoder_1_out20), .Q(register_20_q), .clk(CLK), .clr(CLR));
  Register #(.width(32), .trigger("falling"), .Select("low")) register_21 (
    .D(Write_data), .en(decoder_1_out21), .Q(register_21_q), .clk(CLK), .clr(CLR));
  Register #(.width(32), .trigger("falling"), .Select("low")) register_22 (
    .D(Write_data), .en(decoder_1_out22), .Q(register_22_q), .clk(CLK), .clr(CLR));
  Register #(.width(32), .trigger("falling"), .Select("low")) register_23 (
    .D(Write_data), .en(decoder_1_out23), .Q(register_23_q), .clk(CLK), .clr(CLR));
  Register #(.width(32), .trigger("falling"), .Select("low")) register_24 (
    .D(Write_data), .en(decoder_1_out24), .Q(register_24_q), .clk(CLK), .clr(CLR));
  Register #(.width(32), .trigger("falling"), .Select("low")) register_25 (
    .D(Write_data), .en(decoder_1_out25), .Q(register_25_q), .clk(CLK), .clr(CLR));
  Register #(.width(32), .trigger("falling"), .Select("low")) register_26 (
    .D(Write_data), .en(decoder_1_out26), .Q(register_26_q), .clk(CLK), .clr(CLR));
  Register #(.width(32), .trigger("falling"), .Select("low")) register_27 (
    .D(Write_data), .en(decoder_1_out27), .Q(register_27_q), .clk(CLK), .clr(CLR));
  Register #(.width(32), .trigger("falling"), .Select("low")) register_28 (
    .D(Write_data), .en(decoder_1_out28), .Q(register_28_q), .clk(CLK), .clr(CLR));
  Register #(.width(32), .trigger("falling"), .Select("low")) register_29 (
    .D(Write_data), .en(decoder_1_out29), .Q(register_29_q), .clk(CLK), .clr(CLR));
  Register #(.width(32), .trigger("falling"), .Select("low")) register_30 (
    .D(Write_data), .en(decoder_1_out30), .Q(register_30_q), .clk(CLK), .clr(CLR));
  Register #(.width(32), .trigger("falling"), .Select("low")) register_31 (
    .D(Write_data), .en(decoder_1_out31), .Q(register_31_q), .clk(CLK), .clr(CLR));
  Multiplexer #(.select(5), .width(32), .enable("false")) multiplexer_1 (
    .in0({32{1'b0}}), .in1(register_1_q), .in2(register_2_q), .in3(register_3_q), .in4(register_4_q),
    .in5(register_5_q), .in6(register_6_q), .in7(register_7_q), .in8(register_8_q), .in9(register_9_q),
    .in10(register_10_q), .in11(register_11_q), .in12(register_12_q), .in13(register_13_q),
    .in14(register_14_q), .in15(register_15_q), .in16(register_16_q), .in17(register_17_q),
    .in18(register_18_q), .in19(register_19_q), .in20(register_20_q), .in21(register_21_q),
    .in22(register_22_q), .in23(register_23_q), .in24(register_24_q), .in25(register_25_q),
    .in26(register_26_q), .in27(register_27_q), .in28(register_28_q), .in29(register_29_q),
    .in30(register_30_q), .in31(register_31_q), .out(Read_Data_1), .sel(Read_Reg_1));
  Multiplexer #(.select(5), .width(32), .enable("false")) multiplexer_2 (
    .in0({32{1'b0}}), .in1(register_1_q), .in2(register_2_q), .in3(register_3_q), .in4(register_4_q),
    .in5(register_5_q), .in6(register_6_q), .in7(register_7_q), .in8(register_8_q), .in9(register_9_q),
    .in10(register_10_q), .in11(register_11_q), .in12(register_12_q), .in13(register_13_q),
    .in14(register_14_q), .in15(register_15_q), .in16(register_16_q), .in17(register_17_q),
    .in18(register_18_q), .in19(register_19_q), .in20(register_20_q), .in21(register_21_q),
    .in22(register_22_q), .in23(register_23_q), .in24(register_24_q), .in25(register_25_q),
    .in26(register_26_q), .in27(register_27_q), .in28(register_28_q), .in29(register_29_q),
    .in30(register_30_q), .in31(register_31_q), .out(Read_Data_2), .sel(Read_Reg_2));
endmodule

module Split_instruction (
  input  [31:0] Instruction,
  output [6:0] Opcode,
  output [2:0] Func3,
  output [6:0] Func7,
  output [4:0] Rd,
  output [4:0] Rs1,
  output [4:0] Rs2,
  output [31:0] Imm_I,
  output [31:0] Imm_S,
  output [31:0] Imm_B,
  output [31:0] Imm_U,
  output [31:0] Imm_J,
  output [11:0] CSR_Specifier
);

  assign Imm_I = {{20{Instruction[31]}}, Instruction[31:20]};  // Bit_Extender bit_extender_1
  assign Imm_S = {{20{Instruction[31]}}, {Instruction[31:25], Instruction[11:7]}};  // Bit_Extender bit_extender_2
  assign Imm_B = {{19{Instruction[31]}}, {Instruction[31], Instruction[7], Instruction[30:25], Instruction[11:8], 1'b0}};  // Bit_Extender bit_extender_3
  assign Imm_J = {{11{Instruction[31]}}, {Instruction[31], Instruction[19:12], Instruction[20], Instruction[30:21], 1'b0}};  // Bit_Extender bit_extender_4

  assign CSR_Specifier = Instruction[31:20];
  assign Func3 = Instruction[14:12];
  assign Func7 = Instruction[31:25];
  assign Imm_U = {Instruction[31:12], {12{1'b0}}};
  assign Opcode = Instruction[6:0];
  assign Rd = Instruction[11:7];
  assign Rs1 = Instruction[19:15];
  assign Rs2 = Instruction[24:20];
endmodule

module ALU (
  input  [31:0] Operand1,
  input  [31:0] Operand2,
  input  [4:0] Operation,
  output [31:0] Result
);

  wire and_2_out, and_3_out, and_4_out, and_5_out, comparator_1_lt, comparator_2_lt, xor_2_out;
  wire [31:0] adder_1_out, adder_2_out, and_1_out, bit_extender_1_out, bit_extender_2_out, divider_1_out,
       divider_1_rem, multiplexer_1_out, multiplexer_2_out, multiplier_1_cout, multiplier_1_out,
       negate_1_out_3, negate_2_out_3, negate_3_out_3, negate_4_out_3, or_1_out, shifter_1_out,
       shifter_2_out, shifter_3_out, subtractor_1_out, subtractor_2_out, xor_1_out;

  Adder #(.width(32)) adder_1 (.a(Operand1), .b(Operand2), .out(adder_1_out));  // open: cin, cout
  Subtractor #(.width(32)) subtractor_1 (.a(Operand1), .b(Operand2), .out(subtractor_1_out));  // open: bin, bout
  assign xor_1_out = Operand1 ^ Operand2;  // XOR_Gate xor_1, 32 bits wide
  assign or_1_out = Operand1 | Operand2;  // OR_Gate or_1, 32 bits wide
  assign and_1_out = Operand1 & Operand2;  // AND_Gate and_1, 32 bits wide
  Shifter #(.width(32)) shifter_1 (.in(Operand1), .\dist (Operand2[4:0]), .out(shifter_1_out));
  Shifter #(.width(32), .shift("lr")) shifter_2 (.in(Operand1), .\dist (Operand2[4:0]), .out(shifter_2_out));
  Shifter #(.width(32), .shift("ar")) shifter_3 (.in(Operand1), .\dist (Operand2[4:0]), .out(shifter_3_out));
  Comparator #(.width(32)) comparator_1 (.a(Operand1), .b(Operand2), .lt(comparator_1_lt));  // open: gt, eq
  assign bit_extender_1_out = {{31{1'b0}}, comparator_1_lt};  // Bit_Extender bit_extender_1
  Comparator #(.width(32), .mode("unsigned")) comparator_2 (
    .a(Operand1), .b(Operand2), .lt(comparator_2_lt));  // open: gt, eq
  assign bit_extender_2_out = {{31{1'b0}}, comparator_2_lt};  // Bit_Extender bit_extender_2
  and and_2 (and_2_out, Operation[0], Operation[1], Operand1[31]);
  and and_3 (and_3_out, ~Operation[0], Operand1[31]);  // AND_Gate
  and and_4 (and_4_out, ~Operation[0], Operand2[31]);  // AND_Gate
  Multiplexer #(.width(32), .enable("false")) multiplexer_1 (
    .in0({32{1'b0}}), .in1(Operand2), .out(multiplexer_1_out), .sel(and_2_out));
  Multiplexer #(.width(32), .enable("false")) multiplexer_2 (
    .in0({32{1'b0}}), .in1(Operand1), .out(multiplexer_2_out), .sel(and_5_out));
  and and_5 (and_5_out, Operand2[31], Operation[1]);
  Negate negate_1 (.Invert(and_3_out), .out_3(negate_1_out_3), .in_2(Operand1));
  Negate negate_2 (.Invert(and_4_out), .out_3(negate_2_out_3), .in_2(Operand2));
  Multiplier #(.width(32)) multiplier_1 (
    .a(Operand1), .b(Operand2), .out(multiplier_1_out), .cout(multiplier_1_cout));  // open: cin
  Adder #(.width(32)) adder_2 (.a(multiplexer_1_out), .b(multiplexer_2_out), .out(adder_2_out));  // open: cin, cout
  xor xor_2 (xor_2_out, and_3_out, and_4_out);
  Divider #(.width(32)) divider_1 (
    .a(negate_1_out_3), .b(negate_2_out_3), .out(divider_1_out), .rem(divider_1_rem));  // open: upper
  Negate negate_3 (.Invert(xor_2_out), .out_3(negate_3_out_3), .in_2(divider_1_out));
  Negate negate_4 (.Invert(and_3_out), .out_3(negate_4_out_3), .in_2(divider_1_rem));
  Subtractor #(.width(32)) subtractor_2 (
    .a(multiplier_1_cout), .b(adder_2_out), .out(subtractor_2_out));  // open: bin, bout
  Multiplexer #(.select(5), .width(32), .enable("false")) multiplexer_3 (
    .in0(adder_1_out), .in1(subtractor_1_out), .in2(xor_1_out), .in3(or_1_out), .in4(and_1_out),
    .in5(shifter_1_out), .in6(shifter_2_out), .in7(shifter_3_out), .in10(bit_extender_1_out),
    .in11(bit_extender_2_out), .in16(multiplier_1_out), .in17(subtractor_2_out), .in18(subtractor_2_out),
    .in19(subtractor_2_out), .in20(negate_3_out_3), .in21(negate_3_out_3), .in22(negate_4_out_3),
    .in23(negate_4_out_3), .out(Result), .sel(Operation));  // open: in8, in9, in12, in13, in14, in15, in24, in25, in26, in27, in28, in29, in30, in31

  // Notes on the sheet:
  //   Signed and unsigned division are implemented using the same circuit, and one of the bits of the operation is used to choose
  //   All types of multiply use the same circuit, the low bits of the operation are used to choose
endmodule

module Negate (
  input  Invert,
  input  [31:0] in_2,
  output [31:0] out_3
);

  wire [31:0] subtractor_1_out;

  Multiplexer #(.width(32), .enable("false")) multiplexer_1 (
    .in0(in_2), .in1(subtractor_1_out), .out(out_3), .sel(Invert));
  Subtractor #(.width(32)) subtractor_1 (.a({32{1'b0}}), .b(in_2), .out(subtractor_1_out));  // open: bin, bout
endmodule

module Control (
  input  [6:0] Opcode,
  input  [2:0] Func3,
  input  [6:0] Func7,
  input  [31:0] Instruction,
  input  [2:0] Flags,
  output [4:0] ALU_op,
  output [1:0] ALU_Src1,
  output [2:0] ALU_Src2,
  output DataSign,
  output [1:0] DataSize,
  output [1:0] DataSrc,
  output RAMWrite,
  output RegWrite,
  output Jump,
  output [1:0] CSR_Op,
  output CSR_Imm,
  output Illegal_instruction,
  output Ecall,
  output Ebreak,
  output Mret
);

  wire [21:21] rom_1_data;

  ROM #(.addrWidth(20), .dataWidth(22), .Select("high")) rom_1 (
    .addr({Flags, Opcode, Func3, Func7}),
    .data({rom_1_data[21], CSR_Imm, CSR_Op, Jump, RegWrite, RAMWrite, DataSrc, DataSize, DataSign, ALU_Src2, ALU_Src1, ALU_op}));
  Comparator #(.width(32)) comparator_1 (.a(Instruction), .b(32'h73), .eq(Ecall));  // open: gt, lt
  Comparator #(.width(32)) comparator_2 (.a(Instruction), .b(32'h100073), .eq(Ebreak));  // open: gt, lt
  Comparator #(.width(32)) comparator_3 (.a(Instruction), .b(32'h30200073), .eq(Mret));  // open: gt, lt
  and and_1 (Illegal_instruction, rom_1_data[21], ~Ecall, ~Ebreak, ~Mret);  // AND_Gate

  // Notes on the sheet:
  //   contents of rom_1 (hex, n*v repeats v):
  //   3072*243000 128*50100 128*50900 128*51100 128*243000 128*50500 128*50d00 11520*243000 128*43000
  //   3968*243000 128*53100 53105 127*253100 128*5310a 128*5310b 128*53102 53106 31*253100 53107 95*253100
  //   128*53103 128*53104 3072*243000 1024*531a0 11264*243000 128*4a200 128*4aa00 128*4b200 16000*243000
  //   53080 53090 30*253080 53081 95*253080 53085 53093 126*253080 5308a 53091 126*253080 5308b 53092
  //   126*253080 53082 53094 126*253080 53086 53095 30*253080 53087 95*253080 53083 53096 126*253080 53084
  //   53097 126*253080 3072*243000 1024*53020 44032*243000 128*43000 128*631e0 256*243000 128*43000
  //   128*631e0 128*43000 128*631e0 3072*243000 128*75100 8064*243000 1024*751c0 3200*243000 128*57000
  //   128*97000 128*d7000 128*243000 128*157000 128*197000 128*1d7000 15360*243000 128*50100 128*50900
  //   128*51100 128*243000 128*50500 128*50d00 11520*243000 128*43000 3968*243000 128*53100 53105
  //   127*253100 128*5310a 128*5310b 128*53102 53106 31*253100 53107 95*253100 128*53103 128*53104
  //   3072*243000 1024*531a0 11264*243000 128*4a200 128*4aa00 128*4b200 16000*243000 53080 53090 30*253080
  //   53081 95*253080 53085 53093 126*253080 5308a 53091 126*253080 5308b 53092 126*253080 53082 53094
  //   126*253080 53086 53095 30*253080 53087 95*253080 53083 53096 126*253080 53084 53097 126*253080
  //   3072*243000 1024*53020 44032*243000 128*43000 128*631e0 256*243000 128*43000 256*631e0 128*43000
  //   3072*243000 128*75100 8064*243000 1024*751c0 3200*243000 128*57000 128*97000 128*d7000 128*243000
  //   128*157000 128*197000 128*1d7000 15360*243000 128*50100 128*50900 128*51100 128*243000 128*50500
  //   128*50d00 11520*243000 128*43000 3968*243000 128*53100 53105 127*253100 128*5310a 128*5310b
  //   128*53102 53106 31*253100 53107 95*253100 128*53103 128*53104 3072*243000 1024*531a0 11264*243000
  //   128*4a200 128*4aa00 128*4b200 16000*243000 53080 53090 30*253080 53081 95*253080 53085 53093
  //   126*253080 5308a 53091 126*253080 5308b 53092 126*253080 53082 53094 126*253080 53086 53095
  //   30*253080 53087 95*253080 53083 53096 126*253080 53084 53097 126*253080 3072*243000 1024*53020
  //   44032*243000 128*43000 128*631e0 256*243000 128*631e0 256*43000 128*631e0 3072*243000 128*75100
  //   8064*243000 1024*751c0 3200*243000 128*57000 128*97000 128*d7000 128*243000 128*157000 128*197000
  //   128*1d7000 15360*243000 128*50100 128*50900 128*51100 128*243000 128*50500 128*50d00 11520*243000
  //   128*43000 3968*243000 128*53100 53105 127*253100 128*5310a 128*5310b 128*53102 53106 31*253100 53107
  //   95*253100 128*53103 128*53104 3072*243000 1024*531a0 11264*243000 128*4a200 128*4aa00 128*4b200
  //   16000*243000 53080 53090 30*253080 53081 95*253080 53085 53093 126*253080 5308a 53091 126*253080
  //   5308b 53092 126*253080 53082 53094 126*253080 53086 53095 30*253080 53087 95*253080 53083 53096
  //   126*253080 53084 53097 126*253080 3072*243000 1024*53020 44032*243000 128*43000 128*631e0 256*243000
  //   128*631e0 128*43000 128*631e0 128*43000 3072*243000 128*75100 8064*243000 1024*751c0 3200*243000
  //   128*57000 128*97000 128*d7000 128*243000 128*157000 128*197000 128*1d7000 15360*243000 128*50100
  //   128*50900 128*51100 128*243000 128*50500 128*50d00 11520*243000 128*43000 3968*243000 128*53100
  //   53105 127*253100 128*5310a 128*5310b 128*53102 53106 31*253100 53107 95*253100 128*53103 128*53104
  //   3072*243000 1024*531a0 11264*243000 128*4a200 128*4aa00 128*4b200 16000*243000 53080 53090 30*253080
  //   53081 95*253080 53085 53093 126*253080 5308a 53091 126*253080 5308b 53092 126*253080 53082 53094
  //   126*253080 53086 53095 30*253080 53087 95*253080 53083 53096 126*253080 53084 53097 126*253080
  //   3072*243000 1024*53020 44032*243000 128*631e0 128*43000 256*243000 128*43000 128*631e0 128*43000
  //   128*631e0 3072*243000 128*75100 8064*243000 1024*751c0 3200*243000 128*57000 128*97000 128*d7000
  //   128*243000 128*157000 128*197000 128*1d7000 15360*243000 128*50100 128*50900 128*51100 128*243000
  //   128*50500 128*50d00 11520*243000 128*43000 3968*243000 128*53100 53105 127*253100 128*5310a
  //   128*5310b 128*53102 53106 31*253100 53107 95*253100 128*53103 128*53104 3072*243000 1024*531a0
  //   11264*243000 128*4a200 128*4aa00 12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
endmodule

module Memory (
  input  I_O_In_Range,
  input  I_O_misaligned,
  input  [31:0] I_O_Data,
  input  [31:0] Write_Data,
  input  [31:0] PC,
  input  [31:0] Data_addr,
  input  CLK,
  input  Write,
  input  [1:0] Data_Src,
  input  Exception,
  input  Signed__Unsigned,
  input  [1:0] Data_size,
  input  CLR_regs,
  output [4:0] Exceptions,
  output I_O_read,
  output [31:0] I_O_Address,
  output [31:0] Data,
  output [31:0] Instruction
);

  wire and_1_out, and_2_out, comparator_1_eq, multiplexer_2_out, nor_1_out, not_1_out,
       split_word_1_misaligned_split;
  wire [1:0] multiplexer_4_out;
  wire [31:0] ram_1_data, replace_part_1_output, split_word_1_output;

  Multiplexer #(.width(32), .enable("false")) multiplexer_1 (.in0(PC), .in1(Data_addr), .out(I_O_Address), .sel(CLK));
  Comparator #(.width(6)) comparator_1 (.a(I_O_Address[31:26]), .b({6{1'b0}}), .eq(comparator_1_eq));  // open: gt, lt
  nor nor_1 (nor_1_out, I_O_In_Range, comparator_1_eq);
  // Probe on multiplexer_2_out
  // Probe on nor_1_out
  // Probe on CLK
  Multiplexer #(.enable("false")) multiplexer_2 (
    .in0(I_O_misaligned), .in1(split_word_1_misaligned_split), .out(multiplexer_2_out), .sel(comparator_1_eq));
  Replace_part replace_part_1 (
    .Replacement(Write_Data), .Address(I_O_Address[1:0]), .Size__Byte_Half_Word(multiplexer_4_out),
    .Output(replace_part_1_output), .Input(ram_1_data));  // open: Misaligned_Replace
  nor nor_2 (I_O_read, Data_Src[1], Data_Src[0]);
  // Probe on I_O_read
  // Probe on Write
  not not_1 (not_1_out, CLK);
  and and_1 (and_1_out, Write, ~Exception);  // AND_Gate
  // Probe on Exceptions[4]
  D_Flip_Flop #(.Pre_Clr_Positions("LEGACY"), .enable("true"), .NewFFLayout("false")) d_ff_1 (
    .clk(CLK), .D(and_2_out), .Q(Exceptions[4]), .reset(CLR_regs));  // open: Qn, preset, en
  and and_2 (and_2_out, ~CLK, nor_1_out);  // AND_Gate
  RAM #(.addrWidth(24), .dataWidth(32), .bus("separate"), .Select("high")) ram_1 (
    .addr(I_O_Address[25:2]), .din(replace_part_1_output), .data(ram_1_data), .str(and_1_out),
    .sel(comparator_1_eq), .clk(not_1_out));  // open: ld, clr
  Multiplexer #(.width(32), .enable("false")) multiplexer_3 (
    .in0(I_O_Data), .in1(split_word_1_output), .out(Data), .sel(comparator_1_eq));
  Split_word split_word_1 (
    .Address(I_O_Address[1:0]), .Size__Byte_Half_Word(multiplexer_4_out),
    .Signed__Unsigned(Signed__Unsigned), .Misaligned_split(split_word_1_misaligned_split),
    .Output(split_word_1_output), .Input(ram_1_data));
  Multiplexer #(.width(2), .enable("false")) multiplexer_4 (
    .in0(2'b10), .in1(Data_size), .out(multiplexer_4_out), .sel(CLK));
  // Probe on Exceptions[3]
  and and_3 (Exceptions[3], CLK, multiplexer_2_out, I_O_read);
  // Probe on Exceptions[2]
  and and_4 (Exceptions[2], CLK, nor_1_out, I_O_read);
  // Probe on Exceptions[1]
  and and_5 (Exceptions[1], CLK, multiplexer_2_out, Write);
  Register #(.width(32), .Select("low")) u_Instruction (
    .D(Data), .Q(Instruction), .clk(CLK), .clr(CLR_regs));  // open: en
  // Probe on Exceptions[0]
  and and_6 (Exceptions[0], CLK, nor_1_out, Write);

  // Notes on the sheet:
  //   Exceptions: Instruction access fault | Load address misaligned | Load access fault | Store address misaligned | Store access fault
endmodule

module CSR (
  input  Interrupt,
  input  [31:0] Val,
  input  [31:0] Cause,
  input  [31:0] PC,
  input  Exception,
  input  Return_from_exception,
  input  [1:0] Pending_interrupts,
  input  [4:0] Rs1_uimm,
  input  [4:0] Rd,
  input  [11:0] CSR_specifier,
  input  [31:0] \time ,
  input  [31:0] timeh,
  input  [31:0] Rs1Val,
  input  [1:0] Operation____RW_RS_RC,
  input  [1:0] DataSrc,
  input  CLK,
  input  CLR,
  input  Imm,
  output Illegal_instruction,
  output [1:0] Interrupts,
  output [31:0] NewPC,
  output Stop_clock,
  output [31:0] Output
);

  wire and_1_out, and_2_out, and_3_out, and_4_out, and_5_out, and_6_out, and_7_out, and_8_out, and_9_out,
       and_10_out, and_11_out, and_12_out, and_13_out, and_14_out, and_15_out, and_16_out, and_18_out,
       and_20_out, and_24_out, and_25_out, and_26_out, comparator_1_eq, comparator_2_eq, comparator_3_eq,
       comparator_4_eq, comparator_5_eq, comparator_6_eq, comparator_7_eq, comparator_8_eq, comparator_9_eq,
       comparator_10_eq, comparator_11_eq, comparator_12_eq, comparator_13_eq, comparator_14_eq,
       comparator_15_eq, comparator_16_eq, comparator_17_eq, comparator_18_eq, comparator_19_eq,
       comparator_20_eq, comparator_21_eq, comparator_22_eq, comparator_23_eq, comparator_24_eq,
       comparator_25_eq, comparator_26_eq, comparator_27_gt, counter_2_carry, counter_4_carry,
       multiplexer_1_out, multiplexer_2_out, nand_1_out, nand_2_out, nor_1_out, nor_2_out, not_2_out,
       not_20_out, or_1_out, or_2_out, or_3_out, or_4_out, or_5_out, or_6_out, or_7_out, or_8_out, or_9_out,
       or_10_out, or_11_out, or_12_out;
  wire [0:0] d_ff_1_q;
  wire [1:0] bit_extender_2_out, not_1_out, register_1_q, register_4_q;
  wire [7:3] MIE_q;
  wire [29:0] adder_1_out, multiplexer_8_out, register_5_q, register_8_q;
  wire [31:0] apply_csr_operation_1_newvalue, bit_extender_1_out, controlled_buffer_1_out, counter_1_q,
       counter_2_q, counter_3_q, counter_4_q, counter_5_q, multiplexer_3_out, multiplexer_4_out,
       multiplexer_5_out, multiplexer_6_out, register_2_q, register_3_q, register_6_q, register_7_q;

  Pull_Resistor pull_resistor_1 (.node(Val));
  // Probe on and_1_out
  // Probe on and_2_out
  nor nor_1 (nor_1_out, Rs1_uimm[0], Rs1_uimm[1], Rs1_uimm[2], Rs1_uimm[3], Rs1_uimm[4]);
  assign bit_extender_1_out = {{27{1'b0}}, Rs1_uimm};  // Bit_Extender bit_extender_1
  nor nor_2 (nor_2_out, Rd[0], Rd[1], Rd[2], Rd[3], Rd[4]);
  // Probe on CLR
  // Probe on CLK
  and and_1 (and_1_out, or_1_out, and_3_out);
  and and_2 (and_2_out, nand_1_out, and_3_out);
  nand nand_1 (nand_1_out, nor_1_out, Operation____RW_RS_RC[1]);
  or or_1 (or_1_out, ~nor_2_out, Operation____RW_RS_RC[1], ~Operation____RW_RS_RC[0]);  // OR_Gate
  // Probe on apply_csr_operation_1_newvalue
  // Probe on CSR_specifier
  Comparator #(.width(12), .mode("unsigned")) comparator_1 (
    .a(12'h300), .b(CSR_specifier), .eq(comparator_1_eq));  // open: gt, lt
  Comparator #(.width(12), .mode("unsigned")) comparator_2 (
    .a(12'h304), .b(CSR_specifier), .eq(comparator_2_eq));  // open: gt, lt
  Comparator #(.width(12), .mode("unsigned")) comparator_3 (
    .a(12'h344), .b(CSR_specifier), .eq(comparator_3_eq));  // open: gt, lt
  Comparator #(.width(12), .mode("unsigned")) comparator_4 (
    .a(12'h301), .b(CSR_specifier), .eq(comparator_4_eq));  // open: gt, lt
  Comparator #(.width(12), .mode("unsigned")) comparator_5 (
    .a(12'h305), .b(CSR_specifier), .eq(comparator_5_eq));  // open: gt, lt
  Comparator #(.width(12), .mode("unsigned")) comparator_6 (
    .a(12'h340), .b(CSR_specifier), .eq(comparator_6_eq));  // open: gt, lt
  Comparator #(.width(12), .mode("unsigned")) comparator_7 (
    .a(12'h341), .b(CSR_specifier), .eq(comparator_7_eq));  // open: gt, lt
  Comparator #(.width(12), .mode("unsigned")) comparator_8 (
    .a(12'h342), .b(CSR_specifier), .eq(comparator_8_eq));  // open: gt, lt
  Comparator #(.width(12), .mode("unsigned")) comparator_9 (
    .a(12'h343), .b(CSR_specifier), .eq(comparator_9_eq));  // open: gt, lt
  Comparator #(.width(12), .mode("unsigned")) comparator_10 (
    .a(12'h7c0), .b(CSR_specifier), .eq(comparator_10_eq));  // open: gt, lt
  Comparator #(.width(12), .mode("unsigned")) comparator_11 (
    .a(12'h800), .b(CSR_specifier), .eq(comparator_11_eq));  // open: gt, lt
  Comparator #(.width(12), .mode("unsigned")) comparator_12 (
    .a(12'h320), .b(CSR_specifier), .eq(comparator_12_eq));  // open: gt, lt
  Comparator #(.width(12), .mode("unsigned")) comparator_13 (
    .a(12'hb00), .b(CSR_specifier), .eq(comparator_13_eq));  // open: gt, lt
  Comparator #(.width(12), .mode("unsigned")) comparator_14 (
    .a(12'hc00), .b(CSR_specifier), .eq(comparator_14_eq));  // open: gt, lt
  Comparator #(.width(12), .mode("unsigned")) comparator_15 (
    .a(12'hb80), .b(CSR_specifier), .eq(comparator_15_eq));  // open: gt, lt
  Comparator #(.width(12), .mode("unsigned")) comparator_16 (
    .a(12'hc80), .b(CSR_specifier), .eq(comparator_16_eq));  // open: gt, lt
  Comparator #(.width(12), .mode("unsigned")) comparator_17 (
    .a(12'hb02), .b(CSR_specifier), .eq(comparator_17_eq));  // open: gt, lt
  Comparator #(.width(12), .mode("unsigned")) comparator_18 (
    .a(12'hc02), .b(CSR_specifier), .eq(comparator_18_eq));  // open: gt, lt
  Comparator #(.width(12), .mode("unsigned")) comparator_19 (
    .a(12'hb82), .b(CSR_specifier), .eq(comparator_19_eq));  // open: gt, lt
  Comparator #(.width(12), .mode("unsigned")) comparator_20 (
    .a(12'hc82), .b(CSR_specifier), .eq(comparator_20_eq));  // open: gt, lt
  assign controlled_buffer_1_out = comparator_21_eq ? \time  : 32'bz;  // Controlled_Buffer controlled_buffer_1
  Comparator #(.width(12), .mode("unsigned")) comparator_21 (
    .a(12'hc01), .b(CSR_specifier), .eq(comparator_21_eq));  // open: gt, lt
  Comparator #(.width(12), .mode("unsigned")) comparator_22 (
    .a(12'hc81), .b(CSR_specifier), .eq(comparator_22_eq));  // open: gt, lt
  assign controlled_buffer_1_out = comparator_22_eq ? timeh : 32'bz;  // Controlled_Buffer controlled_buffer_2
  Comparator #(.width(12), .mode("unsigned")) comparator_23 (
    .a(12'hf11), .b(CSR_specifier), .eq(comparator_23_eq));  // open: gt, lt
  Comparator #(.width(12), .mode("unsigned")) comparator_24 (
    .a(12'hf12), .b(CSR_specifier), .eq(comparator_24_eq));  // open: gt, lt
  Comparator #(.width(12), .mode("unsigned")) comparator_25 (
    .a(12'hf13), .b(CSR_specifier), .eq(comparator_25_eq));  // open: gt, lt
  Comparator #(.width(12), .mode("unsigned")) comparator_26 (
    .a(12'hf14), .b(CSR_specifier), .eq(comparator_26_eq));  // open: gt, lt
  and and_3 (and_3_out, DataSrc[1], DataSrc[0]);
  or or_2 (or_2_out, Return_from_exception, Exception, and_4_out);
  and and_4 (and_4_out, and_2_out, comparator_1_eq);
  Register #(.width(2), .trigger("falling"), .Select("low")) register_1 (
    .D({apply_csr_operation_1_newvalue[11], apply_csr_operation_1_newvalue[7]}), .en(and_5_out),
    .Q(register_1_q), .clk(CLK), .clr(CLR));
  and and_5 (and_5_out, and_2_out, comparator_2_eq);
  and and_6 (and_6_out, and_2_out, comparator_5_eq);
  Register #(.width(32), .trigger("falling"), .Select("low")) register_2 (
    .D(apply_csr_operation_1_newvalue), .en(and_7_out), .Q(register_2_q), .clk(CLK), .clr(CLR));
  and and_7 (and_7_out, and_2_out, comparator_6_eq);
  and and_8 (and_8_out, and_2_out, comparator_7_eq);
  or or_3 (or_3_out, and_8_out, Exception);
  and and_9 (and_9_out, and_2_out, comparator_8_eq);
  or or_4 (or_4_out, and_9_out, Exception);
  and and_10 (and_10_out, and_2_out, comparator_9_eq);
  or or_5 (or_5_out, and_10_out, Exception);
  or or_6 (or_6_out, comparator_27_gt, and_11_out);
  and and_11 (and_11_out, and_2_out, comparator_10_eq);
  Register #(.width(32), .trigger("falling"), .Select("low")) register_3 (
    .D(apply_csr_operation_1_newvalue), .en(and_12_out), .Q(register_3_q), .clk(CLK), .clr(CLR));
  and and_12 (and_12_out, and_2_out, comparator_11_eq);
  Register #(.width(2), .trigger("falling"), .Select("low")) register_4 (
    .D({apply_csr_operation_1_newvalue[2], apply_csr_operation_1_newvalue[0]}), .en(and_13_out),
    .Q(register_4_q), .clk(CLK), .clr(CLR));
  and and_13 (and_13_out, and_2_out, comparator_12_eq);
  assign not_1_out = ~register_4_q;  // NOT_Gate not_1, 2 bits wide
  and and_14 (and_14_out, and_2_out, comparator_13_eq);
  or or_7 (or_7_out, comparator_13_eq, comparator_14_eq);
  and and_15 (and_15_out, comparator_14_eq, and_2_out);
  and and_16 (and_16_out, and_2_out, comparator_15_eq);
  or or_8 (or_8_out, comparator_15_eq, comparator_16_eq);
  and and_17 (and_15_out, comparator_16_eq, and_2_out);
  and and_18 (and_18_out, and_2_out, comparator_17_eq);
  or or_9 (or_9_out, comparator_17_eq, comparator_18_eq);
  and and_19 (and_15_out, comparator_18_eq, and_2_out);
  and and_20 (and_20_out, and_2_out, comparator_19_eq);
  or or_10 (or_10_out, comparator_19_eq, comparator_20_eq);
  and and_21 (and_15_out, comparator_20_eq, and_2_out);
  and and_22 (and_15_out, and_2_out, or_11_out);
  or or_11 (or_11_out, comparator_21_eq, comparator_22_eq);
  or or_12 (or_12_out, comparator_23_eq, comparator_24_eq, comparator_25_eq, comparator_26_eq);
  Multiplexer #(.select(2), .enable("false")) multiplexer_1 (
    .in0(apply_csr_operation_1_newvalue[7]), .in1(MIE_q[3]), .in2(1'b0), .in3(MIE_q[7]),
    .out(multiplexer_1_out), .sel({Return_from_exception, Exception}));
  Multiplexer #(.select(2), .enable("false")) multiplexer_2 (
    .in0(apply_csr_operation_1_newvalue[3]), .in1(1'b0), .in2(MIE_q[7]), .in3(MIE_q[3]),
    .out(multiplexer_2_out), .sel({Return_from_exception, Exception}));
  assign bit_extender_2_out = {{1{MIE_q[3]}}, MIE_q[3]};  // Bit_Extender bit_extender_2
  assign Interrupts = bit_extender_2_out & Pending_interrupts & register_1_q;  // AND_Gate and_23, 2 bits wide
  D_Flip_Flop #(.trigger("falling"), .Pre_Clr_Positions("LEGACY"), .enable("true"), .NewFFLayout("false")) d_ff_1 (
    .clk(CLK), .D(apply_csr_operation_1_newvalue[0]), .Q(d_ff_1_q[0]), .en(and_6_out), .reset(CLR));  // open: Qn, preset
  Register #(.width(30), .trigger("falling"), .Select("low")) register_5 (
    .D(apply_csr_operation_1_newvalue[31:2]), .en(and_6_out), .Q(register_5_q), .clk(CLK), .clr(CLR));
  assign controlled_buffer_1_out = comparator_6_eq ? register_2_q : 32'bz;  // Controlled_Buffer controlled_buffer_3
  Multiplexer #(.width(32), .enable("false")) multiplexer_3 (
    .in0(apply_csr_operation_1_newvalue), .in1(PC), .out(multiplexer_3_out), .sel(Exception));
  Multiplexer #(.width(32), .enable("false")) multiplexer_4 (
    .in0(apply_csr_operation_1_newvalue), .in1({Interrupt, Cause[30:0]}), .out(multiplexer_4_out),
    .sel(Exception));
  Register #(.width(32), .trigger("falling"), .Select("low")) register_6 (
    .D(multiplexer_4_out), .en(or_4_out), .Q(register_6_q), .clk(CLK), .clr(CLR));
  Multiplexer #(.width(32), .enable("false")) multiplexer_5 (
    .in0(apply_csr_operation_1_newvalue), .in1(Val), .out(multiplexer_5_out), .sel(Exception));
  Register #(.width(32), .trigger("falling"), .Select("low")) register_7 (
    .D(multiplexer_5_out), .en(or_5_out), .Q(register_7_q), .clk(CLK), .clr(CLR));
  Counter #(.width(32), .max('hffffffff), .trigger("falling")) counter_1 (
    .load(and_11_out), .D(apply_csr_operation_1_newvalue), .count(or_6_out), .Q(counter_1_q),
    .carry(Stop_clock), .clk(CLK), .preset(CLR), .down(1'b1));  // open: clr
  assign controlled_buffer_1_out = comparator_10_eq ? counter_1_q : 32'bz;  // Controlled_Buffer controlled_buffer_4
  assign controlled_buffer_1_out = comparator_11_eq ? register_3_q : 32'bz;  // Controlled_Buffer controlled_buffer_5
  assign controlled_buffer_1_out = comparator_12_eq ? {{29{1'b0}}, register_4_q[1], 1'b0, register_4_q[0]} : 32'bz;  // Controlled_Buffer controlled_buffer_6
  assign controlled_buffer_1_out = or_7_out ? counter_2_q : 32'bz;  // Controlled_Buffer controlled_buffer_7
  Counter #(.width(32), .max('hffffffff), .trigger("falling")) counter_2 (
    .load(and_14_out), .D(apply_csr_operation_1_newvalue), .count(not_1_out[0]), .Q(counter_2_q),
    .carry(counter_2_carry), .clk(CLK), .clr(CLR));  // open: preset, down
  and and_24 (and_24_out, not_1_out[0], counter_2_carry);
  Counter #(.width(32), .max('hffffffff), .trigger("falling")) counter_3 (
    .load(and_16_out), .D(apply_csr_operation_1_newvalue), .count(and_24_out), .Q(counter_3_q), .clk(CLK),
    .clr(CLR));  // open: carry, preset, down
  assign controlled_buffer_1_out = or_8_out ? counter_3_q : 32'bz;  // Controlled_Buffer controlled_buffer_8
  Counter #(.width(32), .max('hffffffff), .trigger("falling")) counter_4 (
    .load(and_18_out), .D(apply_csr_operation_1_newvalue), .count(not_1_out[1]), .Q(counter_4_q),
    .carry(counter_4_carry), .clk(CLK), .clr(CLR));  // open: preset, down
  assign controlled_buffer_1_out = or_9_out ? counter_4_q : 32'bz;  // Controlled_Buffer controlled_buffer_9
  and and_25 (and_25_out, not_1_out[1], counter_4_carry);
  Counter #(.width(32), .max('hffffffff), .trigger("falling")) counter_5 (
    .load(and_20_out), .D(apply_csr_operation_1_newvalue), .count(and_25_out), .Q(counter_5_q), .clk(CLK),
    .clr(CLR));  // open: carry, preset, down
  assign controlled_buffer_1_out = or_10_out ? counter_5_q : 32'bz;  // Controlled_Buffer controlled_buffer_10
  assign controlled_buffer_1_out = or_12_out ? {32{1'b0}} : 32'bz;  // Controlled_Buffer controlled_buffer_11
  Apply_CSR_operation apply_csr_operation_1 (
    .NewValue(apply_csr_operation_1_newvalue), .PreviousValue(controlled_buffer_1_out),
    .Operation(Operation____RW_RS_RC), .InputValue(multiplexer_6_out));
  Multiplexer #(.width(32), .enable("false")) multiplexer_6 (
    .in0(Rs1Val), .in1(bit_extender_1_out), .out(multiplexer_6_out), .sel(Imm));
  D_Flip_Flop #(.trigger("falling"), .Pre_Clr_Positions("LEGACY"), .enable("true"), .NewFFLayout("false")) MPIE (
    .clk(CLK), .D(multiplexer_1_out), .Q(MIE_q[7]), .en(or_2_out), .reset(CLR));  // open: Qn, preset
  D_Flip_Flop #(.trigger("falling"), .Pre_Clr_Positions("LEGACY"), .enable("true"), .NewFFLayout("false")) MIE (
    .clk(CLK), .D(multiplexer_2_out), .Q(MIE_q[3]), .en(or_2_out), .reset(CLR));  // open: Qn, preset
  assign controlled_buffer_1_out = comparator_4_eq ? 32'h880001 : 32'bz;  // Controlled_Buffer controlled_buffer_12
  assign controlled_buffer_1_out = comparator_5_eq ? {register_5_q, 1'b0, d_ff_1_q[0]} : 32'bz;  // Controlled_Buffer controlled_buffer_13
  Register #(.width(30), .trigger("falling"), .Select("low")) register_8 (
    .D(multiplexer_3_out[31:2]), .en(or_3_out), .Q(register_8_q), .clk(CLK), .clr(CLR));
  assign controlled_buffer_1_out = comparator_8_eq ? register_6_q : 32'bz;  // Controlled_Buffer controlled_buffer_14
  assign controlled_buffer_1_out = comparator_9_eq ? register_7_q : 32'bz;  // Controlled_Buffer controlled_buffer_15
  Comparator #(.width(32), .mode("unsigned")) comparator_27 (
    .a({32{1'b1}}), .b(counter_1_q), .gt(comparator_27_gt));  // open: eq, lt
  // Probe on and_15_out
  assign controlled_buffer_1_out = comparator_1_eq ? {{24{1'b0}}, MIE_q[7], 3'b000, MIE_q[3], 3'b000} : 32'bz;  // Controlled_Buffer controlled_buffer_16
  assign controlled_buffer_1_out = comparator_2_eq ? {{20{1'b0}}, register_1_q[1], 3'b000, register_1_q[0], {7{1'b0}}} : 32'bz;  // Controlled_Buffer controlled_buffer_17
  assign controlled_buffer_1_out = comparator_3_eq ? {{20{1'b0}}, Pending_interrupts[1], 3'b000, Pending_interrupts[0], {7{1'b0}}} : 32'bz;  // Controlled_Buffer controlled_buffer_18
  assign controlled_buffer_1_out = comparator_7_eq ? {register_8_q, 2'b00} : 32'bz;  // Controlled_Buffer controlled_buffer_19
  not not_2 (not_2_out, comparator_1_eq);
  not not_3 (not_2_out, comparator_2_eq);
  not not_4 (not_2_out, comparator_3_eq);
  not not_5 (not_2_out, comparator_4_eq);
  not not_6 (not_2_out, comparator_5_eq);
  not not_7 (not_2_out, comparator_6_eq);
  not not_8 (not_2_out, comparator_7_eq);
  not not_9 (not_2_out, comparator_8_eq);
  not not_10 (not_2_out, comparator_9_eq);
  not not_11 (not_2_out, comparator_10_eq);
  not not_12 (not_2_out, comparator_11_eq);
  not not_13 (not_2_out, comparator_12_eq);
  not not_14 (not_2_out, or_7_out);
  not not_15 (not_2_out, or_8_out);
  not not_16 (not_2_out, or_9_out);
  not not_17 (not_2_out, or_10_out);
  not not_18 (not_2_out, or_11_out);
  not not_19 (not_2_out, or_12_out);
  Pull_Resistor pull_resistor_2 (.node(controlled_buffer_1_out));
  or or_13 (Illegal_instruction, and_15_out, and_26_out);
  and and_26 (and_26_out, not_2_out, and_3_out);
  Pull_Resistor pull_resistor_3 (.node(and_15_out));
  Pull_Resistor #(.pull(1)) pull_resistor_4 (.node(not_2_out));
  // Probe on not_2_out
  nand nand_2 (nand_2_out, Interrupt, d_ff_1_q[0]);
  Adder #(.width(30)) adder_1 (.a(Cause[29:0]), .b(register_5_q), .out(adder_1_out));  // open: cin, cout
  Multiplexer #(.width(32), .enable("false")) multiplexer_7 (
    .in0({32{1'b0}}), .in1(controlled_buffer_1_out), .out(Output), .sel(and_1_out));
  Multiplexer #(.width(30), .enable("false")) multiplexer_8 (
    .in0(adder_1_out), .in1(register_5_q), .out(multiplexer_8_out), .sel(nand_2_out));
  not not_20 (not_20_out, Exception);
  Multiplexer #(.width(32), .enable("false")) multiplexer_9 (
    .in0({multiplexer_8_out, 2'b00}), .in1({register_8_q, 2'b00}), .out(NewPC), .sel(not_20_out));

  // Notes on the sheet:
  //   Cause does not include interrupt bit, only exception code
  //   SrcZero
  //   DestZero
  //   Read
  //   Write
  //   Using CSR
  //   XLEN: 32
  //   0
  //   Extensions
  //   and_15 drives only 1 and floats otherwise
  //   and_17 drives only 1 and floats otherwise
  //   and_19 drives only 1 and floats otherwise
  //   and_21 drives only 1 and floats otherwise
  //   and_22 drives only 1 and floats otherwise
  //   mstatus
  //   mscratch
  //   ureg00
  //   time
  //   timeh
  //   mvenderid, marchid, mimpid, mhartid
  //   mie
  //   mip
  //   misa
  //   mtvec
  //   mepc
  //   mcause
  //   mtval
  //   debug
  //   mcountinhibit
  //   cycle, mcycle
  //   cycleh, mcycleh
  //   instret, minstret
  //   instreth, minstreth
  //   not_2 drives only 0 and floats otherwise
  //   not_3 drives only 0 and floats otherwise
  //   not_4 drives only 0 and floats otherwise
  //   not_5 drives only 0 and floats otherwise
  //   not_6 drives only 0 and floats otherwise
  //   not_7 drives only 0 and floats otherwise
  //   not_8 drives only 0 and floats otherwise
  //   not_9 drives only 0 and floats otherwise
  //   not_10 drives only 0 and floats otherwise
  //   not_11 drives only 0 and floats otherwise
  //   not_12 drives only 0 and floats otherwise
  //   not_13 drives only 0 and floats otherwise
  //   not_14 drives only 0 and floats otherwise
  //   not_15 drives only 0 and floats otherwise
  //   not_16 drives only 0 and floats otherwise
  //   not_17 drives only 0 and floats otherwise
  //   not_18 drives only 0 and floats otherwise
  //   not_19 drives only 0 and floats otherwise
endmodule

module I_O (
  input  Keyboard_Available,
  input  [15:0] Keyboard_Data,
  input  [31:0] Data_in,
  input  [31:0] Address,
  input  Read,
  input  CLK,
  input  CLR,
  input  Write,
  input  [1:0] DataSize,
  output CLK_2,
  output Enable_Keyboard,
  output CLR_2,
  output [15:0] TTY_Data,
  output CLK_3,
  output Enable_TTY,
  output CLR_3,
  output [31:0] Screen_1,
  output [31:0] Screen_2,
  output [31:0] Screen_3,
  output [31:0] Screen_4,
  output [31:0] Screen_5,
  output [31:0] Screen_6,
  output [31:0] Screen_7,
  output [31:0] Screen_8,
  output [31:0] Screen_9,
  output [31:0] Screen_10,
  output [31:0] Screen_11,
  output [31:0] Screen_12,
  output [31:0] Screen_13,
  output [31:0] Screen_14,
  output [31:0] Screen_15,
  output [31:0] Screen_16,
  output [31:0] Screen_17,
  output [31:0] Screen_18,
  output [31:0] Screen_19,
  output [31:0] Screen_20,
  output [31:0] Screen_21,
  output [31:0] Screen_22,
  output [31:0] Screen_23,
  output [31:0] Screen_24,
  output [31:0] Screen_25,
  output [31:0] Screen_26,
  output [31:0] Screen_27,
  output [31:0] Screen_28,
  output [31:0] Screen_29,
  output [31:0] Screen_30,
  output [31:0] Screen_31,
  output [31:0] Screen_32,
  output [1:0] Pending_interrupts,
  output [31:0] Data_out,
  output In_range,
  output Misaligned,
  output [31:0] \time ,
  output [31:0] timeh
);

  wire and_5_out, and_6_out, and_7_out, and_8_out, and_10_out, and_11_out, comparator_1_eq, comparator_2_eq,
       comparator_3_eq, comparator_4_eq, comparator_5_gt, comparator_6_eq, comparator_6_gt, comparator_7_eq,
       decoder_1_out0, decoder_1_out1, decoder_1_out2, decoder_1_out3, decoder_1_out4, decoder_1_out5,
       decoder_1_out6, decoder_1_out7, decoder_1_out8, decoder_1_out9, decoder_1_out10, decoder_1_out11,
       decoder_1_out12, decoder_1_out13, decoder_1_out14, decoder_1_out15, decoder_1_out16, decoder_1_out17,
       decoder_1_out18, decoder_1_out19, decoder_1_out20, decoder_1_out21, decoder_1_out22, decoder_1_out23,
       decoder_1_out24, decoder_1_out25, decoder_1_out26, decoder_1_out27, decoder_1_out28, decoder_1_out29,
       decoder_1_out30, decoder_1_out31;
  wire [31:0] bit_extender_1_out, multiplexer_1_out, register_33_q, register_34_q;

  Pull_Resistor pull_resistor_1 (.node(Misaligned));
  Pull_Resistor pull_resistor_2 (.node(In_range));
  Pull_Resistor pull_resistor_3 (.node(Data_out));
  and and_1 (Enable_Keyboard, comparator_1_eq, Read, ~Write);  // AND_Gate
  Comparator #(.width(32)) comparator_1 (.a(32'hf0000080), .b(Address), .eq(comparator_1_eq));  // open: gt, lt
  buf buffer_1 (In_range, comparator_1_eq);
  and and_2 (Enable_TTY, comparator_1_eq, Write);
  assign bit_extender_1_out = {{16{1'b0}}, Keyboard_Data};  // Bit_Extender bit_extender_1
  assign Data_out = Enable_Keyboard ? bit_extender_1_out : 32'bz;  // Controlled_Buffer controlled_buffer_1
  Comparator #(.width(25)) comparator_2 (.a(Address[31:7]), .b(25'h1e00000), .eq(comparator_2_eq));  // open: gt, lt
  Comparator #(.width(2)) comparator_3 (.a(2'b10), .b(DataSize), .eq(comparator_3_eq));  // open: gt, lt
  and and_3 (Misaligned, ~comparator_3_eq, comparator_2_eq);  // AND_Gate
  and and_4 (In_range, Write, comparator_2_eq);
  Register #(.width(32), .trigger("falling"), .Select("low")) register_1 (
    .D(Data_in), .en(decoder_1_out0), .Q(Screen_1), .clk(CLK), .clr(CLR));
  Decoder #(.select(5), .disabled(0)) decoder_1 (
    .out0(decoder_1_out0), .out1(decoder_1_out1), .out2(decoder_1_out2), .out3(decoder_1_out3),
    .out4(decoder_1_out4), .out5(decoder_1_out5), .out6(decoder_1_out6), .out7(decoder_1_out7),
    .out8(decoder_1_out8), .out9(decoder_1_out9), .out10(decoder_1_out10), .out11(decoder_1_out11),
    .out12(decoder_1_out12), .out13(decoder_1_out13), .out14(decoder_1_out14), .out15(decoder_1_out15),
    .out16(decoder_1_out16), .out17(decoder_1_out17), .out18(decoder_1_out18), .out19(decoder_1_out19),
    .out20(decoder_1_out20), .out21(decoder_1_out21), .out22(decoder_1_out22), .out23(decoder_1_out23),
    .out24(decoder_1_out24), .out25(decoder_1_out25), .out26(decoder_1_out26), .out27(decoder_1_out27),
    .out28(decoder_1_out28), .out29(decoder_1_out29), .out30(decoder_1_out30), .out31(decoder_1_out31),
    .sel(Address[6:2]), .en(and_5_out));
  and and_5 (and_5_out, comparator_2_eq, Write, comparator_3_eq);
  Register #(.width(32), .trigger("falling"), .Select("low")) register_2 (
    .D(Data_in), .en(decoder_1_out1), .Q(Screen_2), .clk(CLK), .clr(CLR));
  Register #(.width(32), .trigger("falling"), .Select("low")) register_3 (
    .D(Data_in), .en(decoder_1_out2), .Q(Screen_3), .clk(CLK), .clr(CLR));
  Register #(.width(32), .trigger("falling"), .Select("low")) register_4 (
    .D(Data_in), .en(decoder_1_out3), .Q(Screen_4), .clk(CLK), .clr(CLR));
  Register #(.width(32), .trigger("falling"), .Select("low")) register_5 (
    .D(Data_in), .en(decoder_1_out4), .Q(Screen_5), .clk(CLK), .clr(CLR));
  Register #(.width(32), .trigger("falling"), .Select("low")) register_6 (
    .D(Data_in), .en(decoder_1_out5), .Q(Screen_6), .clk(CLK), .clr(CLR));
  Register #(.width(32), .trigger("falling"), .Select("low")) register_7 (
    .D(Data_in), .en(decoder_1_out6), .Q(Screen_7), .clk(CLK), .clr(CLR));
  Register #(.width(32), .trigger("falling"), .Select("low")) register_8 (
    .D(Data_in), .en(decoder_1_out7), .Q(Screen_8), .clk(CLK), .clr(CLR));
  Register #(.width(32), .trigger("falling"), .Select("low")) register_9 (
    .D(Data_in), .en(decoder_1_out8), .Q(Screen_9), .clk(CLK), .clr(CLR));
  Register #(.width(32), .trigger("falling"), .Select("low")) register_10 (
    .D(Data_in), .en(decoder_1_out9), .Q(Screen_10), .clk(CLK), .clr(CLR));
  Register #(.width(32), .trigger("falling"), .Select("low")) register_11 (
    .D(Data_in), .en(decoder_1_out10), .Q(Screen_11), .clk(CLK), .clr(CLR));
  Register #(.width(32), .trigger("falling"), .Select("low")) register_12 (
    .D(Data_in), .en(decoder_1_out11), .Q(Screen_12), .clk(CLK), .clr(CLR));
  Register #(.width(32), .trigger("falling"), .Select("low")) register_13 (
    .D(Data_in), .en(decoder_1_out12), .Q(Screen_13), .clk(CLK), .clr(CLR));
  Register #(.width(32), .trigger("falling"), .Select("low")) register_14 (
    .D(Data_in), .en(decoder_1_out13), .Q(Screen_14), .clk(CLK), .clr(CLR));
  Register #(.width(32), .trigger("falling"), .Select("low")) register_15 (
    .D(Data_in), .en(decoder_1_out14), .Q(Screen_15), .clk(CLK), .clr(CLR));
  Register #(.width(32), .trigger("falling"), .Select("low")) register_16 (
    .D(Data_in), .en(decoder_1_out15), .Q(Screen_16), .clk(CLK), .clr(CLR));
  Register #(.width(32), .trigger("falling"), .Select("low")) register_17 (
    .D(Data_in), .en(decoder_1_out16), .Q(Screen_17), .clk(CLK), .clr(CLR));
  Register #(.width(32), .trigger("falling"), .Select("low")) register_18 (
    .D(Data_in), .en(decoder_1_out17), .Q(Screen_18), .clk(CLK), .clr(CLR));
  Register #(.width(32), .trigger("falling"), .Select("low")) register_19 (
    .D(Data_in), .en(decoder_1_out18), .Q(Screen_19), .clk(CLK), .clr(CLR));
  Register #(.width(32), .trigger("falling"), .Select("low")) register_20 (
    .D(Data_in), .en(decoder_1_out19), .Q(Screen_20), .clk(CLK), .clr(CLR));
  Register #(.width(32), .trigger("falling"), .Select("low")) register_21 (
    .D(Data_in), .en(decoder_1_out20), .Q(Screen_21), .clk(CLK), .clr(CLR));
  Register #(.width(32), .trigger("falling"), .Select("low")) register_22 (
    .D(Data_in), .en(decoder_1_out21), .Q(Screen_22), .clk(CLK), .clr(CLR));
  Register #(.width(32), .trigger("falling"), .Select("low")) register_23 (
    .D(Data_in), .en(decoder_1_out22), .Q(Screen_23), .clk(CLK), .clr(CLR));
  Register #(.width(32), .trigger("falling"), .Select("low")) register_24 (
    .D(Data_in), .en(decoder_1_out23), .Q(Screen_24), .clk(CLK), .clr(CLR));
  Register #(.width(32), .trigger("falling"), .Select("low")) register_25 (
    .D(Data_in), .en(decoder_1_out24), .Q(Screen_25), .clk(CLK), .clr(CLR));
  Register #(.width(32), .trigger("falling"), .Select("low")) register_26 (
    .D(Data_in), .en(decoder_1_out25), .Q(Screen_26), .clk(CLK), .clr(CLR));
  Register #(.width(32), .trigger("falling"), .Select("low")) register_27 (
    .D(Data_in), .en(decoder_1_out26), .Q(Screen_27), .clk(CLK), .clr(CLR));
  Register #(.width(32), .trigger("falling"), .Select("low")) register_28 (
    .D(Data_in), .en(decoder_1_out27), .Q(Screen_28), .clk(CLK), .clr(CLR));
  Register #(.width(32), .trigger("falling"), .Select("low")) register_29 (
    .D(Data_in), .en(decoder_1_out28), .Q(Screen_29), .clk(CLK), .clr(CLR));
  Register #(.width(32), .trigger("falling"), .Select("low")) register_30 (
    .D(Data_in), .en(decoder_1_out29), .Q(Screen_30), .clk(CLK), .clr(CLR));
  Register #(.width(32), .trigger("falling"), .Select("low")) register_31 (
    .D(Data_in), .en(decoder_1_out30), .Q(Screen_31), .clk(CLK), .clr(CLR));
  Register #(.width(32), .trigger("falling"), .Select("low")) register_32 (
    .D(Data_in), .en(decoder_1_out31), .Q(Screen_32), .clk(CLK), .clr(CLR));
  and and_6 (and_6_out, ~Address[3], comparator_4_eq, Write);  // AND_Gate
  \time  time_1 (
    .CLR(CLR), .CLK(CLK), .Write(and_6_out), .data_in(Data_in), .L_H(Address[2]), .\time (\time ),
    .timeh(timeh));
  Comparator #(.width(28)) comparator_4 (.a(28'hf000009), .b(Address[31:4]), .eq(comparator_4_eq));  // open: gt, lt
  buf buffer_2 (In_range, comparator_4_eq);
  assign Data_out = and_7_out ? multiplexer_1_out : 32'bz;  // Controlled_Buffer controlled_buffer_2
  and and_7 (and_7_out, comparator_4_eq, Read);
  Multiplexer #(.select(2), .width(32), .enable("false")) multiplexer_1 (
    .in0(\time ), .in1(timeh), .in2(register_33_q), .in3(register_34_q), .out(multiplexer_1_out),
    .sel(Address[3:2]));
  Comparator #(.width(32), .mode("unsigned")) comparator_5 (
    .a(\time ), .b(register_33_q), .gt(comparator_5_gt));  // open: eq, lt
  and and_8 (and_8_out, ~comparator_5_gt, comparator_6_eq);  // AND_Gate
  Comparator #(.width(32), .mode("unsigned")) comparator_6 (
    .a(timeh), .b(register_34_q), .gt(comparator_6_gt), .eq(comparator_6_eq));  // open: lt
  or or_1 (Pending_interrupts[0], and_8_out, comparator_6_gt);
  // Probe on Pending_interrupts[0]
  Comparator #(.width(2)) comparator_7 (.a(2'b10), .b(DataSize), .eq(comparator_7_eq));  // open: gt, lt
  and and_9 (Misaligned, ~comparator_7_eq, comparator_4_eq);  // AND_Gate
  Register #(.width(32), .trigger("falling"), .Select("low")) register_33 (
    .D(Data_in), .en(and_10_out), .Q(register_33_q), .clk(CLK), .preset(CLR));  // open: clr, cs
  and and_10 (and_10_out, Address[3], comparator_4_eq, ~Address[2], Write);  // AND_Gate
  and and_11 (and_11_out, Address[3], comparator_4_eq, Address[2], Write);
  Register #(.width(32), .trigger("falling"), .Select("low")) register_34 (
    .D(Data_in), .en(and_11_out), .Q(register_34_q), .clk(CLK), .preset(CLR));  // open: clr, cs

  assign CLK_2 = CLK;
  assign CLK_3 = CLK;
  assign CLR_2 = CLR;
  assign CLR_3 = CLR;
  assign Pending_interrupts[1] = Keyboard_Available;
  assign TTY_Data = Data_in[15:0];

  // Notes on the sheet:
  //   buffer_1 drives only 1 and floats otherwise
  //   and_3 drives only 1 and floats otherwise
  //   and_4 drives only 1 and floats otherwise
  //   mtime
  //   mtime/mtimecmp
  //   buffer_2 drives only 1 and floats otherwise
  //   and_9 drives only 1 and floats otherwise
  //   mtimecmp
  //   Pending interrupts: external interrupt | timer interrupt
endmodule

module Compare (
  input  [31:0] Rs1,
  input  [31:0] Rs2,
  output [2:0] Flags
);

  Comparator #(.width(32)) comparator_1 (.a(Rs1), .b(Rs2), .eq(Flags[2]), .lt(Flags[1]));  // open: gt
  Comparator #(.width(32), .mode("unsigned")) comparator_2 (.a(Rs1), .b(Rs2), .lt(Flags[0]));  // open: gt, eq
endmodule

module Add_4 (
  input  [31:0] Input,
  output [31:0] Output
);

  Adder #(.width(32)) adder_1 (.a(Input), .b(32'h4), .out(Output));  // open: cin, cout
endmodule

module Split_word (
  input  [1:0] Size__Byte_Half_Word,
  input  Signed__Unsigned,
  input  [1:0] Address,
  input  [31:0] Input,
  output Misaligned_split,
  output [31:0] Output
);

  wire or_1_out;
  wire [7:0] multiplexer_1_out;
  wire [15:0] multiplexer_4_out;
  wire [31:0] bit_extender_1_out, bit_extender_2_out, bit_extender_3_out, bit_extender_4_out,
       multiplexer_2_out, multiplexer_6_out;

  assign bit_extender_1_out = {{24{multiplexer_1_out[7]}}, multiplexer_1_out};  // Bit_Extender bit_extender_1
  Multiplexer #(.select(2), .width(8), .enable("false")) multiplexer_1 (
    .in0(Input[7:0]), .in1(Input[15:8]), .in2(Input[23:16]), .in3(Input[31:24]), .out(multiplexer_1_out),
    .sel(Address));
  Multiplexer #(.width(32), .enable("false")) multiplexer_2 (
    .in0(bit_extender_1_out), .in1(bit_extender_2_out), .out(multiplexer_2_out), .sel(Signed__Unsigned));
  assign bit_extender_2_out = {{24{1'b0}}, multiplexer_1_out};  // Bit_Extender bit_extender_2
  Multiplexer #(.select(2), .enable("false")) multiplexer_3 (
    .in0(1'b0), .in1(Address[0]), .in2(or_1_out), .out(Misaligned_split), .sel(Size__Byte_Half_Word));  // open: in3
  assign bit_extender_3_out = {{16{multiplexer_4_out[15]}}, multiplexer_4_out};  // Bit_Extender bit_extender_3
  Multiplexer #(.width(16), .enable("false")) multiplexer_4 (
    .in0(Input[15:0]), .in1(Input[31:16]), .out(multiplexer_4_out), .sel(Address[1]));
  Multiplexer #(.select(2), .width(32), .enable("false")) multiplexer_5 (
    .in0(multiplexer_2_out), .in1(multiplexer_6_out), .in2(Input), .out(Output), .sel(Size__Byte_Half_Word));  // open: in3
  Multiplexer #(.width(32), .enable("false")) multiplexer_6 (
    .in0(bit_extender_3_out), .in1(bit_extender_4_out), .out(multiplexer_6_out), .sel(Signed__Unsigned));
  assign bit_extender_4_out = {{16{1'b0}}, multiplexer_4_out};  // Bit_Extender bit_extender_4
  or or_1 (or_1_out, Address[0], Address[1]);

  // Notes on the sheet:
  //   Byte
  //   Half
  //   Word
endmodule

module Replace_part (
  input  [1:0] Size__Byte_Half_Word,
  input  [31:0] Replacement,
  input  [1:0] Address,
  input  [31:0] Input,
  output Misaligned_Replace,
  output [31:0] Output
);

  wire decoder_1_out0, decoder_1_out1, decoder_1_out2, decoder_1_out3, or_1_out;
  wire [7:0] multiplexer_2_out, multiplexer_3_out, multiplexer_4_out, multiplexer_5_out;
  wire [15:0] multiplexer_6_out, multiplexer_8_out;

  Decoder #(.select(2), .enable("false")) decoder_1 (
    .out0(decoder_1_out0), .out1(decoder_1_out1), .out2(decoder_1_out2), .out3(decoder_1_out3), .sel(Address));
  Multiplexer #(.select(2), .enable("false")) multiplexer_1 (
    .in0(1'b0), .in1(Address[0]), .in2(or_1_out), .out(Misaligned_Replace), .sel(Size__Byte_Half_Word));  // open: in3
  or or_1 (or_1_out, Address[0], Address[1]);
  Multiplexer #(.width(8), .enable("false")) multiplexer_2 (
    .in0(Input[31:24]), .in1(Replacement[7:0]), .out(multiplexer_2_out), .sel(decoder_1_out3));
  Multiplexer #(.width(8), .enable("false")) multiplexer_3 (
    .in0(Input[23:16]), .in1(Replacement[7:0]), .out(multiplexer_3_out), .sel(decoder_1_out2));
  Multiplexer #(.width(8), .enable("false")) multiplexer_4 (
    .in0(Input[15:8]), .in1(Replacement[7:0]), .out(multiplexer_4_out), .sel(decoder_1_out1));
  Multiplexer #(.width(8), .enable("false")) multiplexer_5 (
    .in0(Input[7:0]), .in1(Replacement[7:0]), .out(multiplexer_5_out), .sel(decoder_1_out0));
  Multiplexer #(.width(16), .enable("false")) multiplexer_6 (
    .in0(Input[31:16]), .in1(Replacement[15:0]), .out(multiplexer_6_out), .sel(Address[1]));
  Multiplexer #(.select(2), .width(32), .enable("false")) multiplexer_7 (
    .in0({multiplexer_2_out, multiplexer_3_out, multiplexer_4_out, multiplexer_5_out}),
    .in1({multiplexer_6_out, multiplexer_8_out}), .in2(Replacement), .out(Output), .sel(Size__Byte_Half_Word));  // open: in3
  Multiplexer #(.width(16), .enable("false")) multiplexer_8 (
    .in0(Replacement[15:0]), .in1(Input[15:0]), .out(multiplexer_8_out), .sel(Address[1]));

  // Notes on the sheet:
  //   Byte
  //   Half
  //   Word
endmodule

module Apply_CSR_operation (
  input  [31:0] PreviousValue,
  input  [1:0] Operation,
  input  [31:0] InputValue,
  output [31:0] NewValue
);

  wire [31:0] and_1_out, or_1_out;

  Multiplexer #(.select(2), .width(32), .enable("false")) multiplexer_1 (
    .in1(InputValue), .in2(or_1_out), .in3(and_1_out), .out(NewValue), .sel(Operation));  // open: in0
  assign or_1_out = PreviousValue | InputValue;  // OR_Gate or_1, 32 bits wide
  assign and_1_out = PreviousValue & ~InputValue;  // AND_Gate and_1, 32 bits wide

  // Notes on the sheet:
  //   Write
  //   Set
  //   Clear
endmodule

module CLK (
  input  Manual,
  input  Stop_clock,
  input  CLR,
  input  Stop,
  input  Start,
  output CLK
);

  wire and_1_out, and_2_out, clock_1_out, d_ff_1_q, or_1_out, or_2_out, s_r_ff_1_qn;

  Clock clock_1 (.out(clock_1_out));
  S_R_Flip_Flop #(.Pre_Clr_Positions("LEGACY"), .enable("true"), .NewFFLayout("false")) s_r_ff_1 (
    .S(Stop_clock), .clk(CLK), .R(1'b0), .Qn(s_r_ff_1_qn), .preset(or_1_out), .reset(Start));  // open: Q, en
  or or_1 (or_1_out, CLR, Stop);
  and and_1 (and_1_out, clock_1_out, s_r_ff_1_qn);
  and and_2 (and_2_out, s_r_ff_1_qn, ~clock_1_out);  // AND_Gate
  or or_2 (or_2_out, and_2_out, CLR);
  xor xor_1 (CLK, d_ff_1_q, Manual);
  D_Flip_Flop #(.enable("true"), .NewFFLayout("false")) d_ff_1 (
    .Q(d_ff_1_q), .preset(and_1_out), .reset(or_2_out));  // open: clk, D, Qn, en
endmodule

module Exceptions (
  input  [31:0] ALUVal,
  input  [31:0] PC,
  input  [31:0] Instruction,
  input  InstrAddrMisaligned,
  input  Ecall,
  input  Ebreak,
  input  IllegalInstr,
  input  CSRIllegal,
  input  [4:0] MemExcept,
  input  [1:0] Interrupts,
  output Interrupt,
  output [31:0] Val,
  output [31:0] Cause,
  output Exception
);

  wire and_2_out, and_3_out, and_4_out, and_5_out, buffer_1_out, buffer_2_out, buffer_3_out, buffer_4_out,
       buffer_5_out, buffer_6_out, buffer_7_out, buffer_8_out, buffer_9_out, buffer_10_out, buffer_11_out,
       buffer_12_out, buffer_13_out, buffer_14_out, buffer_15_out, buffer_16_out, buffer_17_out,
       buffer_18_out, buffer_19_out, buffer_20_out, buffer_21_out, buffer_22_out, buffer_23_out,
       buffer_24_out, buffer_25_out, buffer_26_out, buffer_27_out, buffer_28_out, buffer_29_out,
       buffer_30_out, buffer_31_out, buffer_32_out, buffer_33_out, buffer_34_out, buffer_35_out,
       buffer_36_out, buffer_37_out, buffer_38_out, buffer_39_out, buffer_40_out, buffer_41_out,
       buffer_42_out, buffer_43_out, buffer_44_out, buffer_45_out, buffer_46_out, buffer_47_out,
       buffer_48_out, buffer_49_out, buffer_50_out, buffer_51_out, buffer_52_out, buffer_53_out,
       buffer_54_out, buffer_55_out, buffer_56_out, buffer_57_out, buffer_58_out, buffer_59_out,
       buffer_60_out, buffer_61_out, buffer_62_out, buffer_63_out, buffer_64_out, pull_resistor_1_node;
  wire [3:0] bitfinder_1_index;
  wire [11:11] or_1_out;
  wire [31:31] rom_1_data;

  or or_1 (or_1_out[11], IllegalInstr, CSRIllegal);
  // Probe on InstrAddrMisaligned
  // Probe on Ecall
  // Probe on Ebreak
  // Probe on or_1_out[11]
  // Probe on MemExcept[0]
  // Probe on MemExcept[1]
  // Probe on MemExcept[2]
  // Probe on MemExcept[3]
  // Probe on MemExcept[4]
  // Probe on Interrupts[0]
  // Probe on Interrupts[1]
  Pull_Resistor pull_resistor_1 (.node(pull_resistor_1_node));
  buf buffer_1 (buffer_1_out, pull_resistor_1_node);
  buf buffer_2 (buffer_2_out, buffer_1_out);
  buf buffer_3 (buffer_3_out, buffer_2_out);
  buf buffer_4 (buffer_4_out, buffer_3_out);
  buf buffer_5 (buffer_5_out, buffer_4_out);
  buf buffer_6 (buffer_6_out, buffer_5_out);
  buf buffer_7 (buffer_7_out, buffer_6_out);
  buf buffer_8 (buffer_8_out, buffer_7_out);
  buf buffer_9 (buffer_9_out, buffer_8_out);
  buf buffer_10 (buffer_10_out, buffer_9_out);
  buf buffer_11 (buffer_11_out, buffer_10_out);
  buf buffer_12 (buffer_12_out, buffer_11_out);
  buf buffer_13 (buffer_13_out, buffer_12_out);
  buf buffer_14 (buffer_14_out, buffer_13_out);
  buf buffer_15 (buffer_15_out, buffer_14_out);
  buf buffer_16 (buffer_16_out, buffer_15_out);
  buf buffer_17 (buffer_17_out, buffer_16_out);
  buf buffer_18 (buffer_18_out, buffer_17_out);
  buf buffer_19 (buffer_19_out, buffer_18_out);
  buf buffer_20 (buffer_20_out, buffer_19_out);
  buf buffer_21 (buffer_21_out, buffer_20_out);
  buf buffer_22 (buffer_22_out, buffer_21_out);
  buf buffer_23 (buffer_23_out, buffer_22_out);
  buf buffer_24 (buffer_24_out, buffer_23_out);
  buf buffer_25 (buffer_25_out, buffer_24_out);
  buf buffer_26 (buffer_26_out, buffer_25_out);
  buf buffer_27 (buffer_27_out, buffer_26_out);
  buf buffer_28 (buffer_28_out, buffer_27_out);
  buf buffer_29 (buffer_29_out, buffer_28_out);
  buf buffer_30 (buffer_30_out, buffer_29_out);
  buf buffer_31 (buffer_31_out, buffer_30_out);
  buf buffer_32 (buffer_32_out, buffer_31_out);
  buf buffer_33 (buffer_33_out, buffer_32_out);
  buf buffer_34 (buffer_34_out, buffer_33_out);
  buf buffer_35 (buffer_35_out, buffer_34_out);
  buf buffer_36 (buffer_36_out, buffer_35_out);
  buf buffer_37 (buffer_37_out, buffer_36_out);
  buf buffer_38 (buffer_38_out, buffer_37_out);
  buf buffer_39 (buffer_39_out, buffer_38_out);
  buf buffer_40 (buffer_40_out, buffer_39_out);
  buf buffer_41 (buffer_41_out, buffer_40_out);
  buf buffer_42 (buffer_42_out, buffer_41_out);
  buf buffer_43 (buffer_43_out, buffer_42_out);
  buf buffer_44 (buffer_44_out, buffer_43_out);
  buf buffer_45 (buffer_45_out, buffer_44_out);
  buf buffer_46 (buffer_46_out, buffer_45_out);
  buf buffer_47 (buffer_47_out, buffer_46_out);
  buf buffer_48 (buffer_48_out, buffer_47_out);
  buf buffer_49 (buffer_49_out, buffer_48_out);
  buf buffer_50 (buffer_50_out, buffer_49_out);
  buf buffer_51 (buffer_51_out, buffer_50_out);
  buf buffer_52 (buffer_52_out, buffer_51_out);
  buf buffer_53 (buffer_53_out, buffer_52_out);
  buf buffer_54 (buffer_54_out, buffer_53_out);
  buf buffer_55 (buffer_55_out, buffer_54_out);
  buf buffer_56 (buffer_56_out, buffer_55_out);
  buf buffer_57 (buffer_57_out, buffer_56_out);
  buf buffer_58 (buffer_58_out, buffer_57_out);
  buf buffer_59 (buffer_59_out, buffer_58_out);
  buf buffer_60 (buffer_60_out, buffer_59_out);
  buf buffer_61 (buffer_61_out, buffer_60_out);
  buf buffer_62 (buffer_62_out, buffer_61_out);
  buf buffer_63 (buffer_63_out, buffer_62_out);
  buf buffer_64 (buffer_64_out, buffer_63_out);
  Multiplexer #(.select(4), .width(32), .enable("false")) multiplexer_1 (
    .in0({32{1'b0}}), .in1({32{1'b0}}), .in2(ALUVal), .in3(ALUVal), .in4(ALUVal), .in5(ALUVal),
    .in6({32{1'b0}}), .in7({32{1'b0}}), .in8({32{1'b0}}), .in9({32{1'b0}}), .in10(ALUVal),
    .in11(Instruction), .in12(PC), .out(Val), .sel(bitfinder_1_index));  // open: in13, in14, in15
  BitFinder #(.width(13), .\type ("high1")) bitfinder_1 (
    .in({MemExcept[4], or_1_out[11], InstrAddrMisaligned, Ecall, 2'b00, Ebreak, MemExcept[1], MemExcept[3], MemExcept[0], MemExcept[2], Interrupts}),
    .index(bitfinder_1_index), .found(pull_resistor_1_node));
  and and_1 (Exception, and_2_out, and_3_out, and_4_out, and_5_out);
  and and_2 (and_2_out, pull_resistor_1_node, buffer_1_out, buffer_1_out, buffer_2_out, buffer_2_out, buffer_3_out, buffer_3_out, buffer_4_out, buffer_4_out, buffer_5_out, buffer_5_out, buffer_6_out, buffer_6_out, buffer_7_out, buffer_7_out, buffer_8_out, buffer_8_out, buffer_9_out, buffer_9_out, buffer_10_out, buffer_10_out, buffer_11_out, buffer_11_out, buffer_12_out, buffer_12_out, buffer_13_out, buffer_13_out, buffer_14_out, buffer_14_out, buffer_15_out, buffer_15_out, buffer_16_out);
  and and_3 (and_3_out, buffer_16_out, buffer_17_out, buffer_17_out, buffer_18_out, buffer_18_out, buffer_19_out, buffer_19_out, buffer_20_out, buffer_20_out, buffer_21_out, buffer_21_out, buffer_22_out, buffer_22_out, buffer_23_out, buffer_23_out, buffer_24_out, buffer_24_out, buffer_25_out, buffer_25_out, buffer_26_out, buffer_26_out, buffer_27_out, buffer_27_out, buffer_28_out, buffer_28_out, buffer_29_out, buffer_29_out, buffer_30_out, buffer_30_out, buffer_31_out, buffer_31_out, buffer_32_out);
  and and_4 (and_4_out, buffer_32_out, buffer_33_out, buffer_33_out, buffer_34_out, buffer_34_out, buffer_35_out, buffer_35_out, buffer_36_out, buffer_36_out, buffer_37_out, buffer_37_out, buffer_38_out, buffer_38_out, buffer_39_out, buffer_39_out, buffer_40_out, buffer_40_out, buffer_41_out, buffer_41_out, buffer_42_out, buffer_42_out, buffer_43_out, buffer_43_out, buffer_44_out, buffer_44_out, buffer_45_out, buffer_45_out, buffer_46_out, buffer_46_out, buffer_47_out, buffer_47_out, buffer_48_out);
  and and_5 (and_5_out, buffer_48_out, buffer_49_out, buffer_49_out, buffer_50_out, buffer_50_out, buffer_51_out, buffer_51_out, buffer_52_out, buffer_52_out, buffer_53_out, buffer_53_out, buffer_54_out, buffer_54_out, buffer_55_out, buffer_55_out, buffer_56_out, buffer_56_out, buffer_57_out, buffer_57_out, buffer_58_out, buffer_58_out, buffer_59_out, buffer_59_out, buffer_60_out, buffer_60_out, buffer_61_out, buffer_61_out, buffer_62_out, buffer_62_out, buffer_63_out, buffer_63_out, buffer_64_out);
  and and_6 (Interrupt, rom_1_data[31], Exception);
  ROM #(.addrWidth(4), .dataWidth(32), .Select("low")) rom_1 (
    .addr(bitfinder_1_index), .data({rom_1_data[31], Cause[30:0]}));

  assign Cause[31] = 1'b0;

  // Notes on the sheet:
  //   First step to enforce priorities
  //   Delay exception until there has been one for a while to avoid oscillation
  //   Second step to get correct cause
  //   contents of rom_1 (hex, n*v repeats v):
  //   80000007 8000000b 5 7 4 6 3 8 9 b 0 2 1 cccccccc cccccccc cccccccc
endmodule

module \time  (
  input  CLR,
  input  CLK,
  input  Write,
  input  [31:0] data_in,
  input  L_H,
  output [31:0] \time ,
  output [31:0] timeh
);

  wire adder_1_cout, clock_1_out, not_1_out, subtractor_1_bout;
  wire [31:0] multiplexer_1_out, multiplexer_2_out, register_1_q, register_2_q, subtractor_1_out,
       subtractor_2_out, time_1_p3, time_1_p4;

  Clock clock_1 (.out(clock_1_out));
  // Time time_1: pin names not known; wires that end beside it: CLK, clock_1_out, time_1_p3, time_1_p4
  Subtractor #(.width(32)) subtractor_1 (
    .a(multiplexer_1_out), .b(time_1_p4), .out(subtractor_1_out), .bout(subtractor_1_bout));  // open: bin
  Register #(.width(32), .trigger("falling"), .Select("low")) register_1 (
    .D(subtractor_1_out), .en(Write), .Q(register_1_q), .clk(clock_1_out), .clr(CLR));
  Multiplexer #(.width(32), .enable("false")) multiplexer_1 (
    .in0(\time ), .in1(data_in), .out(multiplexer_1_out), .sel(not_1_out));
  Multiplexer #(.width(32), .enable("false")) multiplexer_2 (
    .in0(data_in), .in1(timeh), .out(multiplexer_2_out), .sel(not_1_out));
  Subtractor #(.width(32)) subtractor_2 (
    .a(multiplexer_2_out), .b(time_1_p3), .out(subtractor_2_out), .bin(subtractor_1_bout));  // open: bout
  Adder #(.width(32)) adder_1 (.a(time_1_p4), .b(register_1_q), .out(\time ), .cout(adder_1_cout));  // open: cin
  Register #(.width(32), .trigger("falling"), .Select("low")) register_2 (
    .D(subtractor_2_out), .en(Write), .Q(register_2_q), .clk(clock_1_out), .clr(CLR));
  not not_1 (not_1_out, L_H);
  Adder #(.width(32)) adder_2 (.a(time_1_p3), .b(register_2_q), .out(timeh), .cin(adder_1_cout));  // open: cout
endmodule

module test (
  input  in_1,
  input  in_2,
  input  in_3,
  input  [2:0] in_4,
  input  in_5,
  input  in_6,
  input  in_7,
  input  in_8,
  input  in_9,
  input  in_10,
  input  in_11,
  input  [2:0] in_12,
  input  in_13,
  input  in_14,
  input  in_15
);

  wire counter_1_carry, counter_2_carry;

  Counter #(.width(3), .max('h7), .behavior("old")) counter_1 (
    .load(in_3), .D(in_4), .count(in_5), .carry(counter_1_carry), .clk(in_6), .clr(in_7), .preset(in_1));  // open: Q
  Counter #(.width(3), .max('h7)) counter_2 (
    .load(in_11), .D(in_12), .count(in_10), .carry(counter_2_carry), .clk(in_14), .clr(in_15), .preset(in_8),
    .down(in_13));  // open: Q
  Counter #(.width(3), .max('h7), .behavior("old")) counter_3 (
    .count(counter_1_carry), .clk(in_6), .clr(in_7), .preset(in_2));  // open: load, D, Q, carry
  Counter #(.width(3), .max('h7)) counter_4 (
    .count(counter_2_carry), .clk(in_14), .clr(in_15), .preset(in_9));  // open: load, D, Q, carry, down
endmodule
